// Logisim project 74_series_computer_schematic.circ as structural Verilog: 10 circuits, main circuit main
module main (
  input  in_1,
  input  in_2,
  input  [7:0] in_3
);

  wire ALU_add_sub, ALU_output_enable, button_1_out, carry, clear, clock, halt, input_complete,
       instruction_register_input_enable, manual_clock_pulse, memory_address_register_input_enable, or_2_out,
       output_register_input_enable, program_counter_increment, program_counter_input_enable,
       program_counter_output_enable, ram_input_enable, ram_output_enable, register_A_input_enable,
       register_A_output_enable, register_B_input_enable, register_B_output_enable, request_user_input,
       user_input_output_enable, user_input_ready;
  wire [2:0] microcode_step;
  wire [7:0] A_register_contents, ALU_result, B_register_contents, bus, instruction_register_contents,
       memory_address_register_contents, output_register_contents, program_counter_contents, undriven;

  Button button_1 (.out(button_1_out));
  Button button_2 (.out(clear));
  Button button_3 (.out(input_complete));
  or or_1 (manual_clock_pulse, in_1, button_1_out);
  // Probe on register_A_input_enable
  // Probe on register_A_output_enable
  // Probe on register_B_input_enable
  // Probe on register_B_output_enable
  // Probe on output_register_input_enable
  // Probe on ALU_output_enable
  // Probe on ALU_add_sub
  // Probe on memory_address_register_input_enable
  // Probe on ram_input_enable
  // Probe on ram_output_enable
  // Probe on request_user_input
  // Probe on user_input_output_enable
  // Probe on program_counter_input_enable
  // Probe on program_counter_output_enable
  // Probe on program_counter_increment
  // Probe on instruction_register_input_enable
  // Probe on halt
  // Probe on clock
  // Probe on user_input_ready
  // Probe on carry
  // Probe on bus
  // Probe on program_counter_contents
  // Probe on A_register_contents
  // Probe on ALU_result
  // Probe on B_register_contents
  // Probe on output_register_contents
  // Probe on memory_address_register_contents
  // Probe on instruction_register_contents
  // Probe on microcode_step
  // Probe on microcode_step
  // Probe on bus
  // Probe on program_counter_contents
  // Probe on A_register_contents
  // Probe on ALU_result
  // Probe on B_register_contents
  // Probe on output_register_contents
  // Probe on memory_address_register_contents
  // Probe on instruction_register_contents
  // Probe on microcode_step
  // Probe on bus
  // Probe on program_counter_contents
  // Probe on A_register_contents
  // Probe on ALU_result
  // Probe on B_register_contents
  // Probe on output_register_contents
  // Probe on memory_address_register_contents
  // Probe on instruction_register_contents
  LED led_1 (.in(undriven[7]));
  LED led_2 (.in(undriven[4]));
  LED led_3 (.in(undriven[3]));
  LED led_4 (.in(undriven[6]));
  LED led_5 (.in(undriven[5]));
  LED led_6 (.in(undriven[1]));
  LED led_7 (.in(undriven[0]));
  LED led_8 (.in(undriven[2]));
  or or_2 (or_2_out, carry, clear);
  clock u_CLOCK (.manual_clock(manual_clock_pulse), .clock_out(clock), .auto_manual_step(in_2), .halt(halt));
  user_input user_input_1 (
    .user_input(in_3), .user_finished(input_complete), .request_user_input(request_user_input),
    .buffered_output(bus), .user_input_ready(user_input_ready), .clear(clear),
    .output_enable(user_input_output_enable));
  program_counter PROGRAM_COUNTER (
    .buffered_input(bus), .increment(program_counter_increment), .clock(clock), .clear(clear),
    .output_enable(program_counter_output_enable), .buffered_output(bus),
    .input_enable(program_counter_input_enable), .contents(program_counter_contents));
  regsiter A_REGISTER (
    .buffered_input(bus), .buffered_output(bus), .content(A_register_contents),
    .input_enable(register_A_input_enable), .clock(clock), .clear(clear),
    .output_enable(register_A_output_enable));
  alu ALU (
    .add_sub(ALU_add_sub), .buffered_result(bus), .A_input(A_register_contents),
    .output_enable(ALU_output_enable), .B_input(B_register_contents), .carry_out(carry),
    .unbuffered_result(ALU_result));
  regsiter B_REGISTER (
    .buffered_input(bus), .buffered_output(bus), .content(B_register_contents),
    .input_enable(register_B_input_enable), .clock(clock), .clear(clear),
    .output_enable(register_B_output_enable));
  regsiter OUTPUT_REGISTER (
    .buffered_input(bus), .buffered_output(bus), .content(output_register_contents),
    .input_enable(output_register_input_enable), .clock(clock), .clear(clear), .output_enable(1'b0));
  regsiter MEMORY_ADDRESS_REGISTER (
    .buffered_input(bus), .buffered_output(bus), .content(memory_address_register_contents),
    .input_enable(memory_address_register_input_enable), .clock(clock), .clear(clear), .output_enable(1'b0));
  RAM RAM (
    .input_enable(ram_input_enable), .address(memory_address_register_contents),
    .output_enable(ram_output_enable), .buffered_input(bus), .clock(clock), .buffered_output(bus));
  regsiter INSTRUCTION_REGISTER (
    .buffered_input(bus), .buffered_output(bus), .content(instruction_register_contents),
    .input_enable(instruction_register_input_enable), .clock(clock), .clear(clear), .output_enable(1'b0));
  instruction_decoder instruction_decoder_1 (
    .register_A_input_enable(register_A_input_enable), .register_A_output_enable(register_A_output_enable),
    .register_B_input_enable(register_B_input_enable), .register_B_output_enable(register_B_output_enable),
    .output_register_input_enable(output_register_input_enable), .alu_output_enable(ALU_output_enable),
    .alu_add_sub(ALU_add_sub), .memory_address_register_input_enable(memory_address_register_input_enable),
    .ram_input_enable(ram_input_enable), .ram_output_enable(ram_output_enable),
    .user_input_request_user_input(request_user_input), .user_input_output_enable(user_input_output_enable),
    .program_counter_load(program_counter_input_enable),
    .program_counter_output_enable(program_counter_output_enable),
    .program_counter_increment(program_counter_increment),
    .instruction_register_input_enable(instruction_register_input_enable), .halt(halt), .clock(clock),
    .clear(clear), .user_input_ready(user_input_ready), .carry(or_2_out),
    .instruction_byte(instruction_register_contents), .microcode_step(microcode_step));

  // Other names for the same wires on the sheet: auto_manual_clock = in_2; user_input[7:0] = in_3

  // Notes on the sheet:
  //   this is needed for getting rid of strange startup error condiitions in logisim
endmodule

module alu (
  input  [7:0] A_input,
  input  output_enable,
  input  add_sub,
  input  [7:0] B_input,
  output [7:0] buffered_result,
  output carry_out,
  output [7:0] unbuffered_result
);

  wire [7:0] xor_1_out;

  assign xor_1_out = {8{add_sub}} ^ B_input;  // XOR_Gate xor_1, 8 bits wide
  Adder adder_1 (.a(A_input), .b(xor_1_out), .out(unbuffered_result), .cin(add_sub), .cout(carry_out));
  assign buffered_result = output_enable ? unbuffered_result : 8'bz;  // Controlled_Buffer controlled_buffer_1
endmodule

module regsiter (
  input  [7:0] buffered_input,
  input  input_enable,
  input  clock,
  input  clear,
  input  output_enable,
  output [7:0] content,
  output [7:0] buffered_output
);

  wire and_1_out;
  wire [7:0] controlled_buffer_1_out;

  assign controlled_buffer_1_out = input_enable ? buffered_input : 8'bz;  // Controlled_Buffer controlled_buffer_1
  Register register_1 (.D(controlled_buffer_1_out), .en(1'b1), .Q(content), .clk(and_1_out), .clr(clear));
  and and_1 (and_1_out, input_enable, clock);
  assign buffered_output = output_enable ? content : 8'bz;  // Controlled_Buffer controlled_buffer_2
endmodule

module clock (
  input  manual_clock,
  input  auto_manual_step,
  input  halt,
  output clock_out
);

  wire auto_clock_out, multiplexer_1_out, not_1_out;

  Clock auto_clock (.out(auto_clock_out));
  Multiplexer multiplexer_1 (
    .in0(auto_clock_out), .in1(manual_clock), .out(multiplexer_1_out), .sel(auto_manual_step), .en(1'b1));
  not not_1 (not_1_out, halt);
  and and_1 (clock_out, multiplexer_1_out, not_1_out);
endmodule

module RAM (
  input  [7:0] buffered_input,
  input  input_enable,
  input  [7:0] address,
  input  clock,
  input  output_enable,
  output [7:0] buffered_output
);

  wire not_1_out;
  wire [7:0] ram_1_data;

  RAM_part ram_1 (.addr(address), .data(ram_1_data), .sel(1'b1), .clk(clock), .ld(not_1_out), .clr(1'b0));
  not not_1 (not_1_out, input_enable);
  assign ram_1_data = input_enable ? buffered_input : 8'bz;  // Controlled_Buffer controlled_buffer_1
  assign buffered_output = output_enable ? ram_1_data : 8'bz;  // Controlled_Buffer controlled_buffer_2
endmodule

module program_counter (
  input  input_enable,
  input  output_enable,
  input  [7:0] buffered_input,
  input  increment,
  input  clock,
  input  clear,
  output [7:0] buffered_output,
  output [7:0] contents
);

  wire [7:0] controlled_buffer_1_out;

  assign controlled_buffer_1_out = input_enable ? buffered_input : 8'bz;  // Controlled_Buffer controlled_buffer_1
  Counter counter_1 (
    .load(input_enable), .D(controlled_buffer_1_out), .count(increment), .Q(contents), .clk(clock),
    .clr(clear));  // open: carry
  assign buffered_output = output_enable ? contents : 8'bz;  // Controlled_Buffer controlled_buffer_2
endmodule

module user_input (
  input  output_enable,
  input  [7:0] user_input,
  input  user_finished,
  input  request_user_input,
  input  clear,
  output [7:0] buffered_output,
  output user_input_ready
);

  wire and_1_out, j_k_ff_1_q, or_1_out;

  and and_1 (and_1_out, j_k_ff_1_q, user_finished);
  assign buffered_output = output_enable ? user_input : 8'bz;  // Controlled_Buffer controlled_buffer_1
  or or_1 (or_1_out, and_1_out, request_user_input);
  J_K_Flip_Flop j_k_ff_1 (
    .J(1'b1), .clk(or_1_out), .K(1'b1), .Q(j_k_ff_1_q), .preset(1'b0), .en(1'b1), .reset(clear));  // open: Qn
  not not_1 (user_input_ready, j_k_ff_1_q);
endmodule

module instruction_decoder (
  input  [7:0] instruction_byte,
  input  clock,
  input  clear,
  input  user_input_ready,
  input  carry,
  output register_A_input_enable,
  output register_A_output_enable,
  output register_B_input_enable,
  output register_B_output_enable,
  output output_register_input_enable,
  output alu_output_enable,
  output alu_add_sub,
  output memory_address_register_input_enable,
  output ram_input_enable,
  output ram_output_enable,
  output user_input_request_user_input,
  output user_input_output_enable,
  output program_counter_load,
  output program_counter_output_enable,
  output program_counter_increment,
  output instruction_register_input_enable,
  output halt,
  output [2:0] microcode_step
);

  wire not_1_out, or_1_out;
  wire [1:1] rom_3_data;
  wire [7:2] rom_1_data;

  not not_1 (not_1_out, clock);
  or or_1 (or_1_out, clear, rom_3_data[1]);
  Counter #(.width(3), .max('h7)) counter_1 (
    .load(1'b0), .D(3'b000), .count(1'b1), .Q(microcode_step), .clk(not_1_out), .clr(or_1_out));  // open: carry
  ROM #(.addrWidth(10)) rom_1 (
    .addr({instruction_byte[4:0], microcode_step, user_input_ready, carry}),
    .data({rom_1_data, register_A_input_enable, register_A_output_enable}));  // open: sel
  ROM #(.addrWidth(10)) rom_2 (
    .addr({instruction_byte[4:0], microcode_step, user_input_ready, carry}),
    .data({register_B_input_enable, register_B_output_enable, output_register_input_enable, alu_output_enable, alu_add_sub, memory_address_register_input_enable, ram_input_enable, ram_output_enable}));  // open: sel
  ROM #(.addrWidth(10)) rom_3 (
    .addr({instruction_byte[4:0], microcode_step, user_input_ready, carry}),
    .data({user_input_request_user_input, user_input_output_enable, program_counter_load, program_counter_output_enable, program_counter_increment, instruction_register_input_enable, rom_3_data[1], halt}));  // open: sel

  // Notes on the sheet:
  //   microcode 2
  //   contents of rom_1 (hex, n*v repeats v):
  //   16*0 4*2 84*0 4*1 28*0 4*2
  //   microcode 1
  //   contents of rom_2 (hex, n*v repeats v):
  //   4*4 4*1 4*4 4*5 4*1 76*0 4*4 4*1 4*20 20*0 4*4 4*1 4*10 84*0 4*4 4*1 4*4 4*5 4*81 204*0 4*4 4*1 0 4
  //   0 4 0 1 0 1 112*0 4*4 4*1 24*0 4*4 4*1
  //   microcode 0
  //   contents of rom_3 (hex, n*v repeats v):
  //   4*10 4*c 4*10 4*8 4*0 4*2 72*0 4*10 4*c 4*0 4*2 16*0 4*10 4*c 4*0 4*2 80*0 4*10 4*c 4*10 4*8 4*0 4*2
  //   200*0 4*10 4*c 8 10 8 10 2 20 2 20 0 2 0 2 108*0 4*10 4*c 4*2 20*0 4*10 4*c 4*1
endmodule

module zero_check (
  input  [7:0] buffered_input,
  input  input_enable,
  output is_zero
);

  wire [7:0] controlled_buffer_1_out;

  assign controlled_buffer_1_out = input_enable ? buffered_input : 8'bz;  // Controlled_Buffer controlled_buffer_1
  Pull_Resistor #(.pull(1)) pull_resistor_1 (.node(controlled_buffer_1_out[2]));
  Pull_Resistor #(.pull(1)) pull_resistor_2 (.node(controlled_buffer_1_out[3]));
  Pull_Resistor #(.pull(1)) pull_resistor_3 (.node(controlled_buffer_1_out[1]));
  Pull_Resistor #(.pull(1)) pull_resistor_4 (.node(controlled_buffer_1_out[0]));
  Pull_Resistor #(.pull(1)) pull_resistor_5 (.node(controlled_buffer_1_out[5]));
  Pull_Resistor #(.pull(1)) pull_resistor_6 (.node(controlled_buffer_1_out[6]));
  Pull_Resistor #(.pull(1)) pull_resistor_7 (.node(controlled_buffer_1_out[7]));
  Pull_Resistor #(.pull(1)) pull_resistor_8 (.node(controlled_buffer_1_out[4]));
  nor nor_1 (is_zero, controlled_buffer_1_out[0], controlled_buffer_1_out[1], controlled_buffer_1_out[2], controlled_buffer_1_out[3], controlled_buffer_1_out[4], controlled_buffer_1_out[5], controlled_buffer_1_out[6], controlled_buffer_1_out[7]);
endmodule

module subtraction_test (
  input  in_1,
  input  [7:0] in_2,
  input  in_3,
  input  [7:0] in_4,
  input  in_5,
  input  [7:0] in_6,
  input  in_7,
  input  [7:0] in_8,
  input  [7:0] A,
  input  in_10,
  input  [7:0] B,
  input  in_12,
  input  add_sub,
  output [7:0] out_14,
  output [7:0] out_15
);

  wire alu_1_carry_out, alu_2_carry_out, alu_3_carry_out;
  wire [7:0] alu_3_buffered_result, alu_4_buffered_result, multiplexer_1_out;

  LED led_1 (.in(alu_1_carry_out));
  LED led_2 (.in(alu_2_carry_out));
  LED led_3 (.in(alu_3_carry_out));
  alu alu_1 (
    .add_sub(in_1), .A_input(in_2), .output_enable(in_3), .B_input(in_4), .carry_out(alu_1_carry_out),
    .unbuffered_result(out_14));  // open: buffered_result
  alu alu_2 (
    .add_sub(in_5), .A_input(in_6), .output_enable(in_7), .B_input(in_8), .carry_out(alu_2_carry_out),
    .unbuffered_result(out_15));  // open: buffered_result
  alu alu_3 (
    .add_sub(in_10), .buffered_result(alu_3_buffered_result), .A_input(A), .output_enable(in_12),
    .B_input(multiplexer_1_out), .carry_out(alu_3_carry_out));  // open: unbuffered_result
  alu alu_4 (
    .add_sub(1'b1), .buffered_result(alu_4_buffered_result), .A_input({8{1'b0}}), .output_enable(1'b1),
    .B_input(B));  // open: carry_out, unbuffered_result
  // Probe on alu_3_buffered_result
  Multiplexer #(.width(8)) multiplexer_1 (
    .in0(B), .in1(alu_4_buffered_result), .out(multiplexer_1_out), .sel(add_sub));  // open: en
  // Probe on multiplexer_1_out
  // Probe on alu_4_buffered_result
  RAM_part ram_1 ();  // open: addr, data, sel, clk, ld, clr
endmodule
