# Fritzing sketch clock (saved by Fritzing 0.9.3b)
breadboards: 1

parts:
  LED3 = LED - 5mm [color="Blue (470nm)" package="5 mm [THT]"]
  LED4 = LED - 5mm [color="Blue (470nm)" package="5 mm [THT]"]
  R16 = Resistor [tolerance=±5% resistance=220 package=THT]
  R17 = Resistor [tolerance=±5% resistance=220 package=THT]
  C14 = Ceramic Capacitor [capacitance=100nF package="100 mil [THT, multilayer]"]
  IC20 = DIP - 14 pins [chip_label=74HCT00 package="DIP (Dual Inline) [THT]"]
  IC21 = DIP - 16 pins [chip_label=74HCT109 package="DIP (Dual Inline) [THT]"]
  IC22 = DIP - 16 pins [chip_label=74HCT109 package="DIP (Dual Inline) [THT]"]
  U3 = 555 Timer [package="DIP8 [THT]"]
  R18 = Resistor [tolerance=±5% resistance=220 package=THT]  # not connected
  R19 = Resistor [tolerance=±5% resistance=220 package=THT]
  C15 = Electrolytic Capacitor [capacitance=1µF package="100 mil [THT, electrolytic]"]
  C17 = Ceramic Capacitor [capacitance=100nF package="100 mil [THT, multilayer]"]
  R20 = Rotary Potentiometer (Small) [maximum_resistance=100kΩ package=THT]
  IC23 = IC, DIP package, 14 pins [chip_label=74HCT02]
  IC24 = DIP - 16 pins [chip_label=74HCT157 package="DIP (Dual Inline) [THT]"]
  C18 = Ceramic Capacitor [capacitance=100nF package="100 mil [THT, multilayer]"]

nets:
  N1: LED3.cathode, R16.Pin_0
  N2: LED3.anode, IC22.1Q
  N3: LED4.cathode, R17.Pin_1
  N4: LED4.anode, IC22.2Q
  GND: R17.Pin_0, C14.0, IC20.GND, IC21._1K, IC21.GND, IC21.2CP, IC21._2K, IC22._1K, IC22.GND, IC22._2K, U3.Ground, C15.-, C17.0, IC23.pin7, IC24.2A, IC24.2B, IC24.GND, IC24.3B, IC24.3A, IC24.4B, IC24.4A, IC24._G, C18.1
  VCC: C14.1, IC20.VCC, IC21._1R, IC21.1J, IC21._1S, IC21._2S, IC21.2J, IC21._2R, IC21.VCC, IC22.1J, IC22._1S, IC22._2S, IC22.2J, IC22.VCC, U3.Reset, U3.Discharge, R19.Pin_0, IC23.pin14, IC24.VCC, C18.0
  N5: IC20.1A, IC20.1B, IC22._1R, IC22._2R, IC23.pin13
  N6: IC20.1Y, IC23.pin9
  N7: IC20.2A, IC20.2B, IC20.3Y, IC22.2CP
  N8: IC20.2Y, IC22.1CP
  N9: IC20.3B, IC20.3A, IC20.4Y
  N10: IC20.4B, IC23.pin2, IC23.pin3, IC24.1Y
  N11: IC20.4A, IC23.pin6, IC23.pin10
  N12: IC21.1CP, U3.Output
  N13: IC21.1Q, IC24.1A
  N14: U3.Trigger, U3.Threshold, C15.+, R20.leg1
  N15: U3.Control_Voltage, C17.1
  N16: R19.Pin_1, R20.wiper
  N17: IC23.pin1, IC23.pin5
  N18: IC23.pin4, IC23.pin8

notes:
  control_clock
  data_clock
  manual_clock_input
  halt
  auto/manual
  reset

custom parts:
  DIP - 14 pins: Quad NAND
  DIP - 16 pins: Dual JK flip flop with set and reset, positive edge trigger
  DIP - 16 pins: Quad 2 line to one line data selectors
