# Fritzing sketch control_unit (saved by Fritzing 0.9.3b)
breadboards: 5

parts:
  IC1 = DIP - 28 pins [chip_label=AT28C256 package="DIP (Dual Inline) [THT]"]
  J1 = female pin header, 7 pins [form="♀ (female)"]
  J2 = female pin header, 8 pins [form="♀ (female)"]
  J3 = female pin header, 7 pins [form="♀ (female)"]
  IC2 = DIP - 28 pins [chip_label=AT28C256 package="DIP (Dual Inline) [THT]"]
  J4 = female pin header, 8 pins [form="♀ (female)"]
  IC7 = DIP - 16 pins [chip_label=74HCT138 package="DIP (Dual Inline) [THT]"]
  LED5 = LED - 5mm [color="Green (555nm)" package="5 mm [THT]"]
  LED6 = LED - 5mm [color="Green (555nm)" package="5 mm [THT]"]
  LED7 = LED - 5mm [color="Green (555nm)" package="5 mm [THT]"]
  LED8 = LED - 5mm [color="Green (555nm)" package="5 mm [THT]"]
  LED9 = LED - 5mm [color="Green (555nm)" package="5 mm [THT]"]
  LED10 = LED - 5mm [color="Green (555nm)" package="5 mm [THT]"]
  LED11 = LED - 5mm [color="Green (555nm)" package="5 mm [THT]"]
  LED12 = LED - 5mm [color="Green (555nm)" package="5 mm [THT]"]
  LED13 = LED - 5mm [color="Green (555nm)" package="5 mm [THT]"]
  LED14 = LED - 5mm [color="Green (555nm)" package="5 mm [THT]"]
  LED15 = LED - 5mm [color="Green (555nm)" package="5 mm [THT]"]
  LED16 = LED - 5mm [color="Green (555nm)" package="5 mm [THT]"]
  LED17 = LED - 5mm [color="Green (555nm)" package="5 mm [THT]"]
  LED18 = LED - 5mm [color="Green (555nm)" package="5 mm [THT]"]
  LED19 = LED - 5mm [color="Green (555nm)" package="5 mm [THT]"]
  LED20 = LED - 5mm [color="Green (555nm)" package="5 mm [THT]"]
  LED21 = LED - 5mm [color="Green (555nm)" package="5 mm [THT]"]
  LED22 = LED - 5mm [color="Green (555nm)" package="5 mm [THT]"]
  LED23 = LED - 5mm [color="Green (555nm)" package="5 mm [THT]"]
  LED24 = LED - 5mm [color="Green (555nm)" package="5 mm [THT]"]
  J7 = female pin header, 8 pins [form="♀ (female)"]
  J8 = female pin header, 4 pins [form="♀ (female)"]
  LED25 = LED - 5mm [color="Yellow (585nm)" package="5 mm [THT]"]
  LED26 = LED - 5mm [color="Yellow (585nm)" package="5 mm [THT]"]
  LED27 = LED - 5mm [color="Yellow (585nm)" package="5 mm [THT]"]
  LED28 = LED - 5mm [color="Yellow (585nm)" package="5 mm [THT]"]
  LED29 = LED - 5mm [color="Yellow (585nm)" package="5 mm [THT]"]
  LED30 = LED - 5mm [color="Yellow (585nm)" package="5 mm [THT]"]
  LED31 = LED - 5mm [color="Yellow (585nm)" package="5 mm [THT]"]
  LED32 = LED - 5mm [color="Yellow (585nm)" package="5 mm [THT]"]
  LED33 = LED - 5mm [color="Yellow (585nm)" package="5 mm [THT]"]
  LED34 = LED - 5mm [color="Yellow (585nm)" package="5 mm [THT]"]
  LED35 = LED - 5mm [color="Yellow (585nm)" package="5 mm [THT]"]
  LED36 = LED - 5mm [color="Yellow (585nm)" package="5 mm [THT]"]
  LED37 = LED - 5mm [color="Yellow (585nm)" package="5 mm [THT]"]
  LED38 = LED - 5mm [color="Yellow (585nm)" package="5 mm [THT]"]
  LED39 = LED - 5mm [color="Yellow (585nm)" package="5 mm [THT]"]
  LED40 = LED - 5mm [color="Yellow (585nm)" package="5 mm [THT]"]
  LED41 = LED - 5mm [color="Yellow (585nm)" package="5 mm [THT]"]
  LED42 = LED - 5mm [color="Yellow (585nm)" package="5 mm [THT]"]
  LED43 = LED - 5mm [color="Yellow (585nm)" package="5 mm [THT]"]
  LED44 = LED - 5mm [color="Yellow (585nm)" package="5 mm [THT]"]
  LED45 = LED - 5mm [color="Yellow (585nm)" package="5 mm [THT]"]
  LED46 = LED - 5mm [color="Yellow (585nm)" package="5 mm [THT]"]
  LED47 = LED - 5mm [color="Yellow (585nm)" package="5 mm [THT]"]
  LED48 = LED - 5mm [color="Yellow (585nm)" package="5 mm [THT]"]
  LED49 = LED - 5mm [color="Yellow (585nm)" package="5 mm [THT]"]
  LED51 = LED - 5mm [color="Yellow (585nm)" package="5 mm [THT]"]
  LED53 = LED - 5mm [color="Yellow (585nm)" package="5 mm [THT]"]
  LED55 = LED - 5mm [color="Yellow (585nm)" package="5 mm [THT]"]
  LED56 = LED - 5mm [color="Yellow (585nm)" package="5 mm [THT]"]
  J13 = female pin header, 8 pins [form="♀ (female)"]
  J14 = female pin header, 8 pins [form="♀ (female)"]
  J15 = female pin header, 8 pins [form="♀ (female)"]
  R1 = Resistor [tolerance=±5% resistance=220 package=THT]
  R2 = Resistor [tolerance=±5% resistance=220 package=THT]
  R3 = Resistor [tolerance=±5% resistance=220 package=THT]
  R4 = Resistor [tolerance=±5% resistance=220 package=THT]
  R5 = Resistor [tolerance=±5% resistance=220 package=THT]
  R6 = Resistor [tolerance=±5% resistance=220 package=THT]
  R7 = Resistor [tolerance=±5% resistance=220 package=THT]
  R8 = Resistor [tolerance=±5% resistance=220 package=THT]
  R9 = Resistor [tolerance=±5% resistance=220 package=THT]
  R10 = Resistor [tolerance=±5% resistance=220 package=THT]
  R11 = Resistor [tolerance=±5% resistance=220 package=THT]
  R12 = Resistor [tolerance=±5% resistance=220 package=THT]
  R13 = Resistor [tolerance=±5% resistance=220 package=THT]
  R14 = Resistor [tolerance=±5% resistance=220 package=THT]
  R15 = Resistor [tolerance=±5% resistance=220 package=THT]
  R16 = Resistor [tolerance=±5% resistance=220 package=THT]
  R17 = Resistor [tolerance=±5% resistance=220 package=THT]
  R18 = Resistor [tolerance=±5% resistance=220 package=THT]
  R19 = Resistor [tolerance=±5% resistance=220 package=THT]
  R20 = Resistor [tolerance=±5% resistance=220 package=THT]
  R21 = Resistor [tolerance=±5% resistance=220 package=THT]
  R22 = Resistor [tolerance=±5% resistance=220 package=THT]
  R23 = Resistor [tolerance=±5% resistance=220 package=THT]
  R24 = Resistor [tolerance=±5% resistance=220 package=THT]
  R25 = Resistor [tolerance=±5% resistance=220 package=THT]
  R26 = Resistor [tolerance=±5% resistance=220 package=THT]
  R27 = Resistor [tolerance=±5% resistance=220 package=THT]
  R29 = Resistor [tolerance=±5% resistance=220 package=THT]
  R31 = Resistor [tolerance=±5% resistance=220 package=THT]
  LED58 = LED - 5mm [color="Yellow (585nm)" package="5 mm [THT]"]
  R32 = Resistor [tolerance=±5% resistance=220 package=THT]
  J16 = female pin header, 6 pins [form="♀ (female)"]
  IC10 = 74HCT377 [chip_label=74HCT377 package="DIP (Dual Inline) [THT]"]
  IC11 = DIP - 16 pins [chip_label=74HCT173 package="DIP (Dual Inline) [THT]"]
  IC12 = DIP - 14 pins [chip_label=74HCT04 package="DIP (Dual Inline) [THT]"]
  IC13 = DIP - 16 pins [chip_label=74HCT161 package="DIP (Dual Inline) [THT]"]
  LED59 = LED - 5mm [color="Green (555nm)" package="5 mm [THT]"]
  LED60 = LED - 5mm [color="Green (555nm)" package="5 mm [THT]"]
  LED61 = LED - 5mm [color="Green (555nm)" package="5 mm [THT]"]
  RESET1 = female pin header, 2 pins [form="♀ (female)"]
  C/U_TIMER_RESET2 = female pin header, 2 pins [form="♀ (female)"]
  C/U_TIMER_RESET3 = female pin header, 2 pins [form="♀ (female)"]
  J17 = female pin header, 8 pins [form="♀ (female)"]
  J18 = female pin header, 8 pins [form="♀ (female)"]
  IC14 = DIP - 28 pins [chip_label=AT28C256 package="DIP (Dual Inline) [THT]"]
  J19 = female pin header, 7 pins [form="♀ (female)"]
  J20 = female pin header, 7 pins [form="♀ (female)"]
  J21 = female pin header, 8 pins [form="♀ (female)"]
  J22 = female pin header, 8 pins [form="♀ (female)"]
  IC15 = DIP - 28 pins [chip_label=AT28C256 package="DIP (Dual Inline) [THT]"]

nets:
  N1: IC1.A14, J1.pin1
  N2: IC1.A12, J1.pin3
  N3: IC1.I/O0, J2.pin8
  N4: IC1.I/O1, J2.pin7
  N5: IC1.I/O2, J2.pin6
  GND: IC1.GND, IC2.GND
  N6: IC1.I/O3, J2.pin5
  N7: IC1.I/O4, J2.pin4
  N8: IC1.I/O5, J2.pin3
  N9: IC1.I/O6, J2.pin2
  N10: IC1.I/O7, J2.pin1
  N11: IC1._CE, IC1._OE, IC2._CE, IC2._OE
  N12: IC1.A10, J1.pin5
  N13: IC1.A11, J1.pin4
  N14: IC1.A9, J1.pin6
  N15: IC1.A8, J1.pin7
  N16: IC1.A13, J1.pin2
  VCC: IC1._WE, IC1.VCC, IC2._WE, IC2.VCC
  N17: J3.pin1, IC2.A14
  N18: J3.pin2, IC2.A13
  N19: J3.pin3, IC2.A12
  N20: J3.pin4, IC2.A11
  N21: J3.pin5, IC2.A10
  N22: J3.pin6, IC2.A9
  N23: J3.pin7, IC2.A8
  N24: IC2.I/O0, J4.pin8
  N25: IC2.I/O1, J4.pin7
  N26: IC2.I/O2, J4.pin6
  N27: IC2.I/O3, J4.pin5
  N28: IC2.I/O4, J4.pin4
  N29: IC2.I/O5, J4.pin3
  N30: IC2.I/O6, J4.pin2
  N31: IC2.I/O7, J4.pin1
  N32: IC7._G2A, IC7._G2B, IC7.GND
  N33: IC7.Y7, LED12.cathode
  N34: IC7.Y6, LED11.cathode
  N35: IC7.Y5, LED10.cathode
  N36: IC7.Y4, LED9.cathode
  N37: IC7.Y3, LED8.cathode
  N38: IC7.Y2, LED7.cathode
  N39: IC7.Y1, LED6.cathode
  N40: IC7.Y0, LED5.cathode
  N41: LED13.anode, J8.pin1
  N42: LED14.anode, J8.pin2
  N43: LED15.anode, J8.pin3
  N44: LED16.anode, J8.pin4
  N45: LED17.anode, J7.pin1
  N46: LED18.anode, J7.pin5
  N47: LED19.anode, J7.pin2
  N48: LED20.anode, J7.pin6
  N49: LED21.anode, J7.pin7
  N50: LED22.anode, J7.pin3
  N51: LED23.anode, J7.pin4
  N52: LED24.anode, J7.pin8
  N53: LED25.cathode, R1.Pin_1
  N54: LED25.anode, J13.pin1
  N55: LED26.cathode, R2.Pin_1
  N56: LED26.anode, J13.pin2
  N57: LED27.cathode, R3.Pin_1
  N58: LED27.anode, J13.pin3
  N59: LED28.cathode, R4.Pin_1
  N60: LED28.anode, J13.pin4
  N61: LED29.cathode, R5.Pin_1
  N62: LED29.anode, J13.pin5
  N63: LED30.cathode, R7.Pin_1
  N64: LED30.anode, J13.pin7
  N65: LED31.cathode, R8.Pin_1
  N66: LED31.anode, J13.pin6
  N67: LED32.cathode, R6.Pin_1
  N68: LED32.anode, J13.pin8
  N69: LED33.cathode, R9.Pin_1
  N70: LED33.anode, J14.pin1
  N71: LED34.cathode, R14.Pin_1
  N72: LED34.anode, J14.pin7
  N73: LED35.cathode, R15.Pin_1
  N74: LED35.anode, J14.pin3
  N75: LED36.cathode, R12.Pin_1
  N76: LED36.anode, J14.pin8
  N77: LED37.cathode, R13.Pin_1
  N78: LED37.anode, J14.pin5
  N79: LED38.cathode, R16.Pin_1
  N80: LED38.anode, J14.pin6
  N81: LED39.cathode, R11.Pin_1
  N82: LED39.anode, J14.pin4
  N83: LED40.cathode, R10.Pin_1
  N84: LED40.anode, J14.pin2
  N85: LED41.cathode, R17.Pin_1
  N86: LED41.anode, J15.pin1
  N87: LED42.cathode, R22.Pin_1
  N88: LED42.anode, J15.pin7
  N89: LED43.cathode, R23.Pin_1
  N90: LED43.anode, J15.pin3
  N91: LED44.cathode, R20.Pin_1
  N92: LED44.anode, J15.pin8
  N93: LED45.cathode, R21.Pin_1
  N94: LED45.anode, J15.pin5
  N95: LED46.cathode, R24.Pin_1
  N96: LED46.anode, J15.pin6
  N97: LED47.cathode, R19.Pin_1
  N98: LED47.anode, J15.pin4
  N99: LED48.cathode, R18.Pin_1
  N100: LED48.anode, J15.pin2
  N101: LED49.cathode, R25.Pin_1
  N102: LED49.anode, J16.pin1
  N103: LED51.cathode, R31.Pin_1
  N104: LED51.anode, J16.pin3
  N105: LED53.cathode, R29.Pin_1
  N106: LED53.anode, J16.pin5
  N107: LED55.cathode, R27.Pin_1
  N108: LED55.anode, J16.pin4
  N109: LED56.cathode, R26.Pin_1
  N110: LED56.anode, J16.pin2
  N111: R1.Pin_0, R2.Pin_0, R3.Pin_0, R4.Pin_0, R5.Pin_0, R6.Pin_0, R7.Pin_0, R8.Pin_0, R9.Pin_0, R10.Pin_0, R11.Pin_0, R12.Pin_0, R13.Pin_0, R14.Pin_0, R15.Pin_0, R16.Pin_0, R17.Pin_0, R18.Pin_0, R19.Pin_0, R20.Pin_0, R21.Pin_0, R22.Pin_0, R23.Pin_0, R24.Pin_0, R25.Pin_0, R26.Pin_0, R27.Pin_0, R29.Pin_0, R31.Pin_0, R32.Pin_0
  N112: LED58.cathode, R32.Pin_1
  N113: LED58.anode, J16.pin6
  GND_2: IC10._CLKEN, IC10.GND, IC11._OE, IC11._OE2, IC11.GND, IC12.2A, IC12.3A, IC12.GND, IC13.P0, IC13.P1, IC13.P2, IC13.P3, IC13.GND
  N114: IC10.1Q, J18.pin8
  N115: IC10.1D, J17.pin8
  N116: IC10.2D, J17.pin7
  N117: IC10.2Q, J18.pin7
  N118: IC10.3Q, J18.pin6
  N119: IC10.3D, J17.pin6
  N120: IC10.4D, J17.pin5
  N121: IC10.4Q, J18.pin5
  N122: IC10.CLK, IC11.CP, IC12.1Y, IC13.CP
  N123: IC10.5Q, J18.pin4
  N124: IC10.5D, J17.pin4
  N125: IC10.6D, J17.pin3
  N126: IC10.6Q, J18.pin3
  N127: IC10.7Q, J18.pin2
  N128: IC10.7D, J17.pin2
  N129: IC10.8D, J17.pin1
  N130: IC10.8Q, J18.pin1
  VCC_2: IC10.VCC, IC11.VCC, IC12.VCC, IC13.TE, IC13.VCC
  N131: IC11._E1, IC11._E2, IC11.MR, IC12.4A, IC12.5A
  N132: IC12.1A, C/U_TIMER_RESET2.pin1, C/U_TIMER_RESET2.pin2
  N133: IC12.6Y, IC13._SPE
  N134: IC12.6A, C/U_TIMER_RESET3.pin1, C/U_TIMER_RESET3.pin2
  N135: IC13._MR, RESET1.pin1, RESET1.pin2
  N136: IC13.Q2, LED59.anode
  N137: IC13.Q1, LED60.anode
  N138: IC13.Q0, LED61.anode
  N139: IC14.A14, J20.pin1
  N140: IC14.A12, J20.pin3
  N141: IC14.I/O0, J22.pin8
  N142: IC14.I/O1, J22.pin7
  N143: IC14.I/O2, J22.pin6
  GND_3: IC14.GND, IC15.GND
  N144: IC14.I/O3, J22.pin5
  N145: IC14.I/O4, J22.pin4
  N146: IC14.I/O5, J22.pin3
  N147: IC14.I/O6, J22.pin2
  N148: IC14.I/O7, J22.pin1
  N149: IC14._CE, IC14._OE, IC15._CE, IC15._OE
  N150: IC14.A10, J20.pin5
  N151: IC14.A11, J20.pin4
  N152: IC14.A9, J20.pin6
  N153: IC14.A8, J20.pin7
  N154: IC14.A13, J20.pin2
  VCC_3: IC14._WE, IC14.VCC, IC15._WE, IC15.VCC
  N155: J19.pin1, IC15.A14
  N156: J19.pin2, IC15.A13
  N157: J19.pin3, IC15.A12
  N158: J19.pin4, IC15.A11
  N159: J19.pin5, IC15.A10
  N160: J19.pin6, IC15.A9
  N161: J19.pin7, IC15.A8
  N162: J21.pin1, IC15.I/O7
  N163: J21.pin2, IC15.I/O6
  N164: J21.pin3, IC15.I/O5
  N165: J21.pin4, IC15.I/O4
  N166: J21.pin5, IC15.I/O3
  N167: J21.pin6, IC15.I/O2
  N168: J21.pin7, IC15.I/O1
  N169: J21.pin8, IC15.I/O0

custom parts:
  DIP - 28 pins: 256kbit EEPROM
  DIP - 16 pins: 3 to 8 decoder
  74HCT377: Octal D-Type flip flops with clock enable 8 bit register
  DIP - 16 pins: 4 bit register
  DIP - 14 pins: Hex Inverter
  DIP - 16 pins: 4 bit synchronous counter with load and asynchronous clear
