// Logisim project 8bit_74_series_computer.circ as structural Verilog: 13 circuits, main circuit main
module main (
  input  Clock_Enable,
  input  External_Internal_clock_select,
  input  Run_Setup_Mode,
  input  Select_prog_data_mem,
  input  [7:0] Setup_address,
  input  [7:0] Setup_data,
  input  Examine_write
);

  wire and_1_out, clock_1_clock, cpu_1_clock_out, cpu_1_out_4, cpu_1_out_5, cpu_1_out_6, not_1_out,
       Reset_out, Single_step_advance_out, Write_setup_data_out;
  wire [7:0] cpu_1_address, cpu_1_data_2, ram_1_current_data;

  not not_1 (not_1_out, Run_Setup_Mode);
  Button Single_step_advance (.out(Single_step_advance_out));
  Button Reset (.out(Reset_out));
  // Probe on Setup_address
  // Probe on Setup_address
  // Probe on Setup_data
  // Probe on Setup_data
  // Probe on ram_1_current_data
  // Probe on ram_1_current_data
  // Probe on ram_1_current_data
  and and_1 (and_1_out, not_1_out, Clock_Enable);
  LED led_1 (.in(Setup_address[5]));
  LED led_2 (.in(Setup_address[6]));
  LED led_3 (.in(Setup_address[7]));
  LED led_4 (.in(Setup_data[5]));
  LED led_5 (.in(Setup_data[6]));
  LED led_6 (.in(Setup_data[7]));
  Button Write_setup_data (.out(Write_setup_data_out));
  LED led_7 (.in(ram_1_current_data[6]));
  LED led_8 (.in(ram_1_current_data[7]));
  LED led_9 (.in(ram_1_current_data[5]));
  LED led_10 (.in(Setup_address[1]));
  LED led_11 (.in(Setup_address[3]));
  LED led_12 (.in(Setup_address[2]));
  LED led_13 (.in(Setup_address[4]));
  LED led_14 (.in(Setup_data[3]));
  LED led_15 (.in(Setup_data[2]));
  LED led_16 (.in(Setup_data[4]));
  LED led_17 (.in(Setup_data[1]));
  LED led_18 (.in(ram_1_current_data[3]));
  LED led_19 (.in(ram_1_current_data[1]));
  LED led_20 (.in(ram_1_current_data[4]));
  LED led_21 (.in(ram_1_current_data[2]));
  Clock clock_1 (
    .enable(and_1_out), .Arduino_Crystal(External_Internal_clock_select),
    .Arduino_clock(Single_step_advance_out), .clock(clock_1_clock));
  LED led_22 (.in(Setup_address[0]));
  LED led_23 (.in(Setup_data[0]));
  LED led_24 (.in(ram_1_current_data[0]));
  // Probe on cpu_1_address
  // Probe on cpu_1_address
  // Probe on cpu_1_data_2
  // Probe on cpu_1_data_2
  CPU cpu_1 (
    .in_2(clock_1_clock), .in_1(Reset_out), .DATA(cpu_1_data_2), .ADDRESS(cpu_1_address),
    .out_4(cpu_1_out_4), .out_5(cpu_1_out_5), .out_6(cpu_1_out_6), .clock_out(cpu_1_clock_out),
    .DATA_2(cpu_1_data_2));
  RAM ram_1 (
    .tristate_data_output(cpu_1_data_2), .current_data(ram_1_current_data), .CPU_write_to_mem(cpu_1_out_5),
    .CPU_read_from_mem(cpu_1_out_6), .run_setup(Run_Setup_Mode), .CPU_clock(cpu_1_clock_out),
    .setup_clock(Write_setup_data_out), .cpu_address(cpu_1_address), .setup_address(Setup_address),
    .cpu_data(cpu_1_data_2), .CPU_prog_data_mem(cpu_1_out_4), .setup_prog_data_mem(Select_prog_data_mem),
    .setup_data(Setup_data), .examine_write(Examine_write));
  // Probe on cpu_1_address
  LED led_25 (.in(cpu_1_address[6]));
  LED led_26 (.in(cpu_1_address[7]));
  // Probe on cpu_1_data_2
  LED led_27 (.in(cpu_1_data_2[6]));
  LED led_28 (.in(cpu_1_data_2[7]));
  LED led_29 (.in(cpu_1_address[3]));
  LED led_30 (.in(cpu_1_address[4]));
  LED led_31 (.in(cpu_1_address[2]));
  LED led_32 (.in(cpu_1_address[5]));
  LED led_33 (.in(cpu_1_data_2[4]));
  LED led_34 (.in(cpu_1_data_2[3]));
  LED led_35 (.in(cpu_1_data_2[2]));
  LED led_36 (.in(cpu_1_data_2[5]));
  LED led_37 (.in(cpu_1_address[1]));
  LED led_38 (.in(cpu_1_address[0]));
  LED led_39 (.in(cpu_1_data_2[0]));
  LED led_40 (.in(cpu_1_data_2[1]));
  Pull_Resistor pull_resistor_1 (.node(cpu_1_data_2));

  // Notes on the sheet:
  //   Only necessary in sim - arduino takes care of this
  //   DEC
  //   HEX
  //   DEC
  //   HEX
  //   BIN
  //   DEC
  //   HEX
  //   BIN
  //   DEC
  //   HEX
  //   BIN
  //   DEC
  //   HEX
endmodule

module Clock (
  input  enable,
  input  Arduino_Crystal,
  input  Arduino_clock,
  output clock
);

  wire Crystal_clock_out, multiplexer_1_out;

  Clock_part Crystal_clock (.out(Crystal_clock_out));
  Multiplexer #(.enable("false")) multiplexer_1 (
    .in0(Arduino_clock), .in1(Crystal_clock_out), .out(multiplexer_1_out), .sel(Arduino_Crystal));
  safe_clock_enable safe_clock_enable_1 (.clock_enable(enable), .clock_in(multiplexer_1_out), .clock_out(clock));
endmodule

module RAM (
  input  run_setup,
  input  [7:0] cpu_data,
  input  [7:0] setup_data,
  input  [7:0] cpu_address,
  input  [7:0] setup_address,
  input  CPU_prog_data_mem,
  input  setup_prog_data_mem,
  input  CPU_write_to_mem,
  input  examine_write,
  input  CPU_read_from_mem,
  input  CPU_clock,
  input  setup_clock,
  output [7:0] current_data,
  output [7:0] tristate_data_output
);

  wire multiplexer_1_out, multiplexer_2_out, multiplexer_6_out, multiplexer_7_out, multiplexer_8_out,
       nand_1_out, not_1_out, safe_clock_enable_1_clock_out;
  wire [7:0] multiplexer_3_out, multiplexer_4_out;
  wire [8:8] multiplexer_5_out;

  nand nand_1 (nand_1_out, CPU_prog_data_mem, cpu_address[3], cpu_address[4], cpu_address[5], cpu_address[6], cpu_address[7]);
  Multiplexer #(.enable("false")) multiplexer_1 (
    .in0(1'b0), .in1(CPU_write_to_mem), .out(multiplexer_1_out), .sel(nand_1_out));
  Multiplexer #(.enable("false")) multiplexer_2 (
    .in0(1'b0), .in1(CPU_read_from_mem), .out(multiplexer_2_out), .sel(nand_1_out));
  Multiplexer #(.width(8), .enable("false")) multiplexer_3 (
    .in0(cpu_data), .in1(setup_data), .out(multiplexer_3_out), .sel(run_setup));
  Multiplexer #(.width(8), .enable("false")) multiplexer_4 (
    .in0(cpu_address), .in1(setup_address), .out(multiplexer_4_out), .sel(run_setup));
  Multiplexer #(.enable("false")) multiplexer_5 (
    .in0(CPU_prog_data_mem), .in1(setup_prog_data_mem), .out(multiplexer_5_out[8]), .sel(run_setup));
  Multiplexer #(.enable("false")) multiplexer_6 (
    .in0(multiplexer_1_out), .in1(examine_write), .out(multiplexer_6_out), .sel(run_setup));
  Multiplexer #(.enable("false")) multiplexer_7 (
    .in0(multiplexer_2_out), .in1(1'b0), .out(multiplexer_7_out), .sel(run_setup));
  Multiplexer #(.enable("false")) multiplexer_8 (
    .in0(CPU_clock), .in1(setup_clock), .out(multiplexer_8_out), .sel(run_setup));
  safe_clock_enable safe_clock_enable_1 (
    .clock_enable(multiplexer_6_out), .clock_in(multiplexer_8_out), .clock_out(safe_clock_enable_1_clock_out));
  RAM_part #(.addrWidth(9)) ram_1 (
    .addr({multiplexer_5_out[8], multiplexer_4_out}), .data(current_data), .sel(1'b1),
    .clk(safe_clock_enable_1_clock_out), .ld(not_1_out), .clr(1'b0));
  assign current_data = multiplexer_6_out ? multiplexer_3_out : 8'bz;  // Controlled_Buffer controlled_buffer_1
  not not_1 (not_1_out, multiplexer_6_out);
  assign tristate_data_output = multiplexer_7_out ? current_data : 8'bz;  // Controlled_Buffer controlled_buffer_2
endmodule

module CPU (
  input  in_1,
  input  in_2,
  input  [7:0] DATA,
  output out_4,
  output out_5,
  output out_6,
  output clock_out,
  output [7:0] DATA_2,
  output [7:0] ADDRESS
);

  wire A_IN, A_OUT, ACC_IN, ACC_OUT, ALU_A_IS_BUS, ALU_C_IN, ALU_CARRYBORROW_FLAG_CLOCKED,
       ALU_CARRYBORROW_FLAG_IMM, ALU_EQUAL_FLAG_CLOCKED, ALU_EQUAL_FLAG_IMM, ALU_M,
       ALU_NEGATIVE_FLAG_CLOCKED, ALU_NEGATIVE_FLAG_IMM, ALU_OUT, ALU_S0, ALU_S1, ALU_S2, ALU_S3,
       ALU_STORE_FLAGS, ALU_STORE_RESULT, ALU_ZERO_FLAG_CLOCKED, ALU_ZERO_FLAG_IMM, B_IN, B_OUT, C_IN, C_OUT,
       CLOCK_HALT, CONTROL_CLOCK, CU_CARRYBORROW_MIRROR, CU_EQUAL_MIRROR, CU_NEGATIVE_MIRROR, CU_STEP_RESET,
       CU_ZERO_MIRROR, IR_IN, j_k_ff_1_q, j_k_ff_1_qn, MAR_IN, nor_1_out, PC_COUNT, PC_IN, PC_OUT,
       safe_clock_enable_1_clock_out, SIM_ONLY_RESET, SP_IN, SP_OUT;
  wire [2:0] CU_MICROCODE_STEP;
  wire [7:0] A, ACC, ALU_RESULT_CLOCKED, ALU_RESULT_IMM, B, BUS, C, CU_INSTRUCTION_MIRROR, IR,
       multiplexer_1_out, PC, SP;

  Button button_1 (.out(SIM_ONLY_RESET));
  LED led_1 (.in(ACC_IN));
  LED led_2 (.in(ACC_OUT));
  LED led_3 (.in(A_IN));
  LED led_4 (.in(A_OUT));
  LED led_5 (.in(B_IN));
  LED led_6 (.in(B_OUT));
  LED led_7 (.in(C_IN));
  LED led_8 (.in(C_OUT));
  LED led_9 (.in(ALU_STORE_RESULT));
  LED led_10 (.in(ALU_STORE_FLAGS));
  LED led_11 (.in(ALU_OUT));
  LED led_12 (.in(ALU_A_IS_BUS));
  LED led_13 (.in(ALU_S0));
  LED led_14 (.in(ALU_S1));
  LED led_15 (.in(ALU_S2));
  LED led_16 (.in(ALU_S3));
  LED led_17 (.in(ALU_M));
  LED led_18 (.in(ALU_C_IN));
  nor nor_1 (nor_1_out, in_1, CLOCK_HALT);
  safe_clock_enable safe_clock_enable_1 (
    .clock_enable(nor_1_out), .clock_in(in_2), .clock_out(safe_clock_enable_1_clock_out));
  LED led_19 (.in(MAR_IN));
  LED led_20 (.in(out_5));
  LED led_21 (.in(out_6));
  LED led_22 (.in(out_4));
  LED led_23 (.in(SP_IN));
  LED led_24 (.in(SP_OUT));
  LED led_25 (.in(PC_IN));
  LED led_26 (.in(PC_OUT));
  LED led_27 (.in(PC_COUNT));
  LED led_28 (.in(IR_IN));
  LED led_29 (.in(CU_STEP_RESET));
  LED led_30 (.in(CLOCK_HALT));
  J_K_Flip_Flop j_k_ff_1 (
    .J(1'b1), .clk(safe_clock_enable_1_clock_out), .K(1'b1), .Q(j_k_ff_1_q), .Qn(j_k_ff_1_qn), .preset(1'b0),
    .en(1'b1), .reset(in_1));
  LED led_31 (.in(BUS[6]));
  LED led_32 (.in(BUS[7]));
  LED led_33 (.in(PC[6]));
  LED led_34 (.in(PC[7]));
  LED led_35 (.in(IR[6]));
  LED led_36 (.in(IR[7]));
  LED led_37 (.in(SP[6]));
  LED led_38 (.in(SP[7]));
  LED led_39 (.in(ACC[7]));
  LED led_40 (.in(ACC[6]));
  LED led_41 (.in(A[6]));
  LED led_42 (.in(A[7]));
  LED led_43 (.in(B[6]));
  LED led_44 (.in(B[7]));
  LED led_45 (.in(C[6]));
  LED led_46 (.in(C[7]));
  LED led_47 (.in(ADDRESS[7]));
  LED led_48 (.in(ADDRESS[6]));
  Control_unit control_unit_1 (
    .ACC_IN(ACC_IN), .ACC_OUT(ACC_OUT), .A_IN(A_IN), .A_OUT(A_OUT), .ALU_STORE_RESULT(ALU_STORE_RESULT),
    .ALU_STORE_FLAGS(ALU_STORE_FLAGS), .ALU_S1(ALU_S1), .ALU_S2(ALU_S2), .ALU_S3(ALU_S3), .ALU_M(ALU_M),
    .ALU_C_IN(ALU_C_IN), .MAR_IN(MAR_IN), .WRITE_TO_MEM(out_5), .IR_IN(IR_IN), .control_clock(CONTROL_CLOCK),
    .clear(in_1), .zero_flag(ALU_ZERO_FLAG_CLOCKED), .instruction(IR), .microcode_step(CU_MICROCODE_STEP),
    .B_IN(B_IN), .B_OUT(B_OUT), .C_IN(C_IN), .C_OUT(C_OUT), .ALU_OUT(ALU_OUT), .ALU_A_IS_BUS(ALU_A_IS_BUS),
    .ALU_S0(ALU_S0), .negative_flag(ALU_NEGATIVE_FLAG_CLOCKED),
    .carryborrow_flag(ALU_CARRYBORROW_FLAG_CLOCKED), .READ_FROM_MEM(out_6), .PROG_DATA_MEM(out_4),
    .SP_IN(SP_IN), .SP_OUT(SP_OUT), .PC_IN(PC_IN), .PC_OUT(PC_OUT), .PC_COUNT(PC_COUNT),
    .mirror_instruction(CU_INSTRUCTION_MIRROR), .sim_only_clear(SIM_ONLY_RESET),
    .equal_flag(ALU_EQUAL_FLAG_CLOCKED), .mirror_zero_flag(CU_ZERO_MIRROR),
    .mirror_negative_flag(CU_NEGATIVE_MIRROR), .mirror_carryborrow_flag(CU_CARRYBORROW_MIRROR),
    .mirror_equal_flag(CU_EQUAL_MIRROR), .CU_STEP_RESET(CU_STEP_RESET), .CLOCK_HALT(CLOCK_HALT));
  register_bus_R MAR (
    .\input (BUS), .content(ADDRESS), .input_enable(MAR_IN), .clock(clock_out), .output_enable(1'b0),
    .sim_only_reset(SIM_ONLY_RESET));  // open: buffered_output
  LED led_49 (.in(BUS[4]));
  LED led_50 (.in(BUS[2]));
  LED led_51 (.in(BUS[5]));
  LED led_52 (.in(BUS[3]));
  LED led_53 (.in(PC[4]));
  LED led_54 (.in(PC[3]));
  LED led_55 (.in(PC[2]));
  LED led_56 (.in(PC[5]));
  LED led_57 (.in(IR[3]));
  LED led_58 (.in(IR[5]));
  LED led_59 (.in(IR[2]));
  LED led_60 (.in(IR[4]));
  LED led_61 (.in(SP[2]));
  LED led_62 (.in(SP[4]));
  LED led_63 (.in(SP[3]));
  LED led_64 (.in(SP[5]));
  LED led_65 (.in(ACC[5]));
  LED led_66 (.in(ACC[4]));
  LED led_67 (.in(ACC[2]));
  LED led_68 (.in(ACC[3]));
  LED led_69 (.in(A[3]));
  LED led_70 (.in(A[5]));
  LED led_71 (.in(A[4]));
  LED led_72 (.in(A[2]));
  LED led_73 (.in(B[4]));
  LED led_74 (.in(B[3]));
  LED led_75 (.in(B[2]));
  LED led_76 (.in(B[5]));
  LED led_77 (.in(C[2]));
  LED led_78 (.in(C[3]));
  LED led_79 (.in(C[4]));
  LED led_80 (.in(C[5]));
  LED led_81 (.in(ADDRESS[4]));
  LED led_82 (.in(ADDRESS[3]));
  LED led_83 (.in(ADDRESS[2]));
  LED led_84 (.in(ADDRESS[5]));
  register_bus_R u_IR (
    .\input (BUS), .buffered_output(BUS), .content(IR), .input_enable(IR_IN), .clock(clock_out),
    .output_enable(1'b0), .sim_only_reset(SIM_ONLY_RESET));
  J_K_Flip_Flop j_k_ff_2 (
    .J(1'b1), .clk(j_k_ff_1_q), .K(1'b1), .Q(clock_out), .preset(1'b0), .en(1'b1), .reset(in_1));  // open: Qn
  // Probe on BUS
  LED led_85 (.in(BUS[0]));
  LED led_86 (.in(BUS[1]));
  // Probe on PC
  LED led_87 (.in(PC[1]));
  LED led_88 (.in(PC[0]));
  // Probe on IR
  LED led_89 (.in(IR[0]));
  LED led_90 (.in(IR[1]));
  // Probe on SP
  LED led_91 (.in(SP[0]));
  LED led_92 (.in(SP[1]));
  // Probe on ACC
  LED led_93 (.in(ACC[1]));
  LED led_94 (.in(ACC[0]));
  // Probe on A
  LED led_95 (.in(A[1]));
  LED led_96 (.in(A[0]));
  // Probe on B
  LED led_97 (.in(B[1]));
  LED led_98 (.in(B[0]));
  // Probe on C
  LED led_99 (.in(C[0]));
  LED led_100 (.in(C[1]));
  // Probe on ADDRESS
  LED led_101 (.in(ADDRESS[1]));
  LED led_102 (.in(ADDRESS[0]));
  J_K_Flip_Flop j_k_ff_3 (
    .J(1'b1), .clk(j_k_ff_1_qn), .K(1'b1), .Q(CONTROL_CLOCK), .preset(1'b0), .en(1'b1), .reset(in_1));  // open: Qn
  // Probe on BUS
  // Probe on BUS
  // Probe on PC
  // Probe on PC
  // Probe on IR
  // Probe on IR
  // Probe on SP
  // Probe on SP
  // Probe on ACC
  // Probe on ACC
  // Probe on A
  // Probe on A
  // Probe on B
  // Probe on B
  // Probe on C
  // Probe on C
  // Probe on ADDRESS
  // Probe on ADDRESS
  assign DATA_2 = out_5 ? BUS : 8'bz;  // Controlled_Buffer controlled_buffer_1
  assign BUS = out_6 ? DATA : 8'bz;  // Controlled_Buffer controlled_buffer_2
  Pull_Resistor pull_resistor_1 (.node(BUS));
  LED led_103 (.in(ALU_RESULT_IMM[6]));
  LED led_104 (.in(ALU_RESULT_IMM[7]));
  LED led_105 (.in(ALU_RESULT_CLOCKED[6]));
  LED led_106 (.in(ALU_RESULT_CLOCKED[7]));
  LED led_107 (.in(ALU_ZERO_FLAG_IMM));
  LED led_108 (.in(ALU_NEGATIVE_FLAG_IMM));
  LED led_109 (.in(ALU_CARRYBORROW_FLAG_IMM));
  LED led_110 (.in(ALU_EQUAL_FLAG_IMM));
  LED led_111 (.in(ALU_ZERO_FLAG_CLOCKED));
  LED led_112 (.in(ALU_NEGATIVE_FLAG_CLOCKED));
  LED led_113 (.in(ALU_CARRYBORROW_FLAG_CLOCKED));
  LED led_114 (.in(ALU_EQUAL_FLAG_CLOCKED));
  LED led_115 (.in(CU_INSTRUCTION_MIRROR[7]));
  LED led_116 (.in(CU_MICROCODE_STEP[2]));
  LED led_117 (.in(CU_ZERO_MIRROR));
  LED led_118 (.in(CU_NEGATIVE_MIRROR));
  LED led_119 (.in(CU_CARRYBORROW_MIRROR));
  LED led_120 (.in(CU_EQUAL_MIRROR));
  LED led_121 (.in(clock_out));
  LED led_122 (.in(CONTROL_CLOCK));
  LED led_123 (.in(ALU_RESULT_IMM[4]));
  LED led_124 (.in(ALU_RESULT_IMM[3]));
  LED led_125 (.in(ALU_RESULT_IMM[2]));
  LED led_126 (.in(ALU_RESULT_IMM[5]));
  LED led_127 (.in(ALU_RESULT_CLOCKED[5]));
  LED led_128 (.in(ALU_RESULT_CLOCKED[4]));
  LED led_129 (.in(ALU_RESULT_CLOCKED[2]));
  LED led_130 (.in(ALU_RESULT_CLOCKED[3]));
  LED led_131 (.in(CU_INSTRUCTION_MIRROR[5]));
  LED led_132 (.in(CU_INSTRUCTION_MIRROR[4]));
  LED led_133 (.in(CU_INSTRUCTION_MIRROR[3]));
  LED led_134 (.in(CU_INSTRUCTION_MIRROR[6]));
  LED led_135 (.in(CU_MICROCODE_STEP[1]));
  LED led_136 (.in(CU_MICROCODE_STEP[0]));
  Multiplexer #(.width(8), .enable("false")) multiplexer_1 (
    .in0(ACC), .in1(BUS), .out(multiplexer_1_out), .sel(ALU_A_IS_BUS));
  // Probe on ALU_RESULT_IMM
  LED led_137 (.in(ALU_RESULT_IMM[1]));
  LED led_138 (.in(ALU_RESULT_IMM[0]));
  // Probe on ALU_RESULT_CLOCKED
  LED led_139 (.in(ALU_RESULT_CLOCKED[0]));
  LED led_140 (.in(ALU_RESULT_CLOCKED[1]));
  LED led_141 (.in(CU_INSTRUCTION_MIRROR[2]));
  LED led_142 (.in(CU_INSTRUCTION_MIRROR[0]));
  LED led_143 (.in(CU_INSTRUCTION_MIRROR[1]));
  program_counter u_PC (
    .\input (BUS), .count(PC_COUNT), .clock(clock_out), .output_enable(PC_OUT), .tristate_output(BUS),
    .in(PC_IN), .contents(PC), .reset(in_1));
  register_bus_L u_ACC (
    .\input (BUS), .buffered_output(BUS), .content(ACC), .output_enable(ACC_OUT), .input_enable(ACC_IN),
    .clock(clock_out), .sim_only_reset(SIM_ONLY_RESET));
  ALU alu_1 (
    .carry_in(ALU_C_IN), .M(ALU_M), .S0(ALU_S0), .S1(ALU_S1), .S2(ALU_S2), .S3(ALU_S3),
    .store_result(ALU_STORE_RESULT), .clock(clock_out), .unclocked_carryborrow_out(ALU_CARRYBORROW_FLAG_IMM),
    .clocked_carryborrow_out(ALU_CARRYBORROW_FLAG_CLOCKED), .unclocked_A___B(ALU_EQUAL_FLAG_IMM),
    .clocked_A___B(ALU_EQUAL_FLAG_CLOCKED), .clocked_zero(ALU_ZERO_FLAG_CLOCKED),
    .unclocked_zero(ALU_ZERO_FLAG_IMM), .tristate_clocked_result(BUS), .A(multiplexer_1_out), .B(BUS),
    .result_output_enable(ALU_OUT), .unclocked_result(ALU_RESULT_IMM), .clocked_result(ALU_RESULT_CLOCKED),
    .unclocked_negative(ALU_NEGATIVE_FLAG_IMM), .clocked_negative(ALU_NEGATIVE_FLAG_CLOCKED),
    .store_flags(ALU_STORE_FLAGS), .sim_only_reset(SIM_ONLY_RESET));
  register_bus_L u_A (
    .\input (BUS), .buffered_output(BUS), .content(A), .output_enable(A_OUT), .input_enable(A_IN),
    .clock(clock_out), .sim_only_reset(SIM_ONLY_RESET));
  register_bus_L u_B (
    .\input (BUS), .buffered_output(BUS), .content(B), .output_enable(B_OUT), .input_enable(B_IN),
    .clock(clock_out), .sim_only_reset(SIM_ONLY_RESET));
  register_bus_L u_C (
    .\input (BUS), .buffered_output(BUS), .content(C), .output_enable(C_OUT), .input_enable(C_IN),
    .clock(clock_out), .sim_only_reset(SIM_ONLY_RESET));
  register_bus_L u_SP (
    .\input (BUS), .buffered_output(BUS), .content(SP), .output_enable(SP_OUT), .input_enable(SP_IN),
    .clock(clock_out), .sim_only_reset(SIM_ONLY_RESET));
  // Probe on ALU_RESULT_IMM
  // Probe on ALU_RESULT_IMM
  // Probe on ALU_RESULT_CLOCKED
  // Probe on ALU_RESULT_CLOCKED
  // Probe on CU_INSTRUCTION_MIRROR
  // Probe on CU_INSTRUCTION_MIRROR
  // Probe on CU_INSTRUCTION_MIRROR
  // Probe on CU_MICROCODE_STEP
  // Probe on CU_MICROCODE_STEP
  // Probe on CU_MICROCODE_STEP

  // Other names for the same wires on the sheet: DATA_CLOCK = clock_out; EXT_CLOCK_PULSE = in_2;
  //   PROG_DATA_MEM = out_4; READ_FROM_MEM = out_6; RESET = in_1; WRITE_TO_MEM = out_5

  // Notes on the sheet:
  //   BIN
  //   BIN
  //   HEX
  //   BIN
  //   HEX
  //   DEC
  //   BIN
  //   HEX
  //   DEC
  //   BIN
  //   HEX
  //   DEC
  //   HEX
  //   DEC
  //   BIN
  //   HEX
  //   DEC
  //   BIN
  //   HEX
  //   DEC
  //   BIN
  //   HEX
  //   DEC
  //   DEC
  //   BIN
  //   HEX
  //   DEC
  //   BIN
  //   HEX
  //   DEC
  //   BIN
  //   HEX
  //   DEC
  //   BIN
  //   HEX
  //   DEC
  //   BIN
  //   HEX
  //   DEC
endmodule

module Control_unit (
  input  [7:0] instruction,
  input  equal_flag,
  input  carryborrow_flag,
  input  negative_flag,
  input  zero_flag,
  input  control_clock,
  input  clear,
  input  sim_only_clear,
  output CLOCK_HALT,
  output CU_STEP_RESET,
  output [7:0] mirror_instruction,
  output IR_IN,
  output PC_COUNT,
  output PC_OUT,
  output PC_IN,
  output SP_OUT,
  output SP_IN,
  output PROG_DATA_MEM,
  output mirror_equal_flag,
  output READ_FROM_MEM,
  output mirror_carryborrow_flag,
  output WRITE_TO_MEM,
  output mirror_negative_flag,
  output MAR_IN,
  output mirror_zero_flag,
  output ALU_C_IN,
  output ALU_M,
  output [2:0] microcode_step,
  output ALU_S3,
  output ALU_S2,
  output ALU_S1,
  output ALU_S0,
  output ALU_A_IS_BUS,
  output ALU_OUT,
  output ALU_STORE_FLAGS,
  output ALU_STORE_RESULT,
  output C_OUT,
  output C_IN,
  output B_OUT,
  output B_IN,
  output A_OUT,
  output A_IN,
  output ACC_OUT,
  output ACC_IN
);

  wire not_1_out;
  wire [7:6] rom_1_data;

  not not_1 (not_1_out, CU_STEP_RESET);
  Register u_mirror_instruction (
    .D(instruction), .en(1'b1), .Q(mirror_instruction), .clk(control_clock), .clr(sim_only_clear));
  Register #(.width(4)) mirror_flags (
    .D({equal_flag, carryborrow_flag, negative_flag, zero_flag}), .en(1'b1),
    .Q({mirror_equal_flag, mirror_carryborrow_flag, mirror_negative_flag, mirror_zero_flag}),
    .clk(control_clock), .clr(sim_only_clear));
  Counter #(.width(3), .max('h7)) microcode_step_counter (
    .load(CU_STEP_RESET), .D(3'b000), .count(not_1_out), .Q(microcode_step), .clk(control_clock), .clr(clear));  // open: carry
  ROM #(.addrWidth(15)) rom_1 (
    .addr({mirror_instruction, mirror_equal_flag, mirror_carryborrow_flag, mirror_negative_flag, mirror_zero_flag, microcode_step}),
    .data({rom_1_data, CLOCK_HALT, CU_STEP_RESET, IR_IN, PC_COUNT, PC_OUT, PC_IN}), .sel(1'b1));
  ROM #(.addrWidth(15)) rom_2 (
    .addr({mirror_instruction, mirror_equal_flag, mirror_carryborrow_flag, mirror_negative_flag, mirror_zero_flag, microcode_step}),
    .data({SP_OUT, SP_IN, PROG_DATA_MEM, READ_FROM_MEM, WRITE_TO_MEM, MAR_IN, ALU_C_IN, ALU_M}), .sel(1'b1));
  ROM #(.addrWidth(15)) rom_3 (
    .addr({mirror_instruction, mirror_equal_flag, mirror_carryborrow_flag, mirror_negative_flag, mirror_zero_flag, microcode_step}),
    .data({ALU_S3, ALU_S2, ALU_S1, ALU_S0, ALU_A_IS_BUS, ALU_OUT, ALU_STORE_FLAGS, ALU_STORE_RESULT}),
    .sel(1'b1));
  ROM #(.addrWidth(15)) rom_4 (
    .addr({mirror_instruction, mirror_equal_flag, mirror_carryborrow_flag, mirror_negative_flag, mirror_zero_flag, microcode_step}),
    .data({C_OUT, C_IN, B_OUT, B_IN, A_OUT, A_IN, ACC_OUT, ACC_IN}), .sel(1'b1));

  // Notes on the sheet:
  //   Common inputs to all EEPROMS
  //   microcode 3
  //   microcode 2
  //   microcode 1
  //   microcode 0
  //   contents of rom_1 (hex, n*v repeats v):
  //   2 c 14 5*0 2 c 2 11 4*0 2 c 14 5*0 2 c 2 11 4*0 2 c 14 5*0 2 c 2 11 4*0 2 c 14 5*0 2 c 2 11 4*0 2 c
  //   14 5*0 2 c 2 11 4*0 2 c 14 5*0 2 c 2 11 4*0 2 c 14 5*0 2 c 2 11 4*0 2 c 14 5*0 2 c 2 11 4*0 2 c 10
  //   5*0 2 c 10 5*0 2 c 10 5*0 2 c 10 5*0 2 c 10 5*0 2 c 10 5*0 2 c 10 5*0 2 c 10 5*0 2 c 10 5*0 2 c 10
  //   5*0 2 c 10 5*0 2 c 10 5*0 2 c 10 5*0 2 c 10 5*0 2 c 10 5*0 2 c 10 5*0 2 c 10 5*0 2 c 10 5*0 2 c 10
  //   5*0 2 c 10 5*0 2 c 10 5*0 2 c 10 5*0 2 c 10 5*0 2 c 10 5*0 2 c 10 5*0 2 c 10 5*0 2 c 10 5*0 2 c 10
  //   5*0 2 c 10 5*0 2 c 10 5*0 2 c 10 5*0 2 c 10 5*0 2 c 10 5*0 2 c 10 5*0 2 c 10 5*0 2 c 10 5*0 2 c 10
  //   5*0 2 c 10 5*0 2 c 10 5*0 2 c 10 5*0 2 c 10 5*0 2 c 10 5*0 2 c 10 5*0 2 c 10 5*0 2 c 10 5*0 2 c 10
  //   5*0 2 c 10 5*0 2 c 10 5*0 2 c 10 5*0 2 c 10 5*0 2 c 10 5*0 2 c 10 5*0 2 c 10 5*0 2 c 10 5*0 2 c 10
  //   5*0 2 c 10 5*0 2 c 10 5*0 2 c 10 5*0 2 c 10 5*0 2 c 10 5*0 2 c 10 5*0 2 c 10 5*0 2 c 10 5*0 2 c 10
  //   5*0 2 c 11 5*0 2 c 11 5*0 2 c 11 5*0 2 c 11 5*0 2 c 11 5*0 2 c 11 5*0 2 c 11 5*0 2 c 11 5*0 2 c 11
  //   5*0 2 c 11 5*0 2 c 11 5*0 2 c 11 5*0 2 c 11 5*0 2 c 11 5*0 2 c 11 5*0 2 c 11 5*0 2 c 6*0 2 c 6*0 2 c
  //   6*0 2 c 6*0 2 c 6*0 2 c 6*0 2 c 6*0 2 c 6*0 2 c 6*0 2 c 6*0 2 c 6*0 2 c 6*0 2 c 6*0 2 c 6*0 2 c 6*0
  //   2 c 6*0 2 c 2 4 14 0 0 0 2 c 2 4 14 0 0 0 2 c 2 4 14 0 0 0 2 c 2 4 14 0 0 0 2 c 2 4 14 0 0 0 2 c 2 4
  //   14 0 0 0 2 c 2 4 14 0 0 0 2 c 2 4 14 0 0 0 2 c 2 4 2 11 0 0 2 c 2 4 2 11 0 0 2 c 2 4 2 11 0 0 2 c 2
  //   4 2 11 0 0 2 c 2 4 2 11 0 0 2 c 2 4 2 11 0 0 2 c 2 4 2 11 0 0 2 c 2 4 2 11 0 0 2 c 10 5*0 2 c 10 5*0
  //   2 c 10 5*0 2 c 10 5*0 2 c 10 5*0 2 c 10 5*0 2 c 10 5*0 2 c 10 5*0 2 c 10 5*0 2 c 10 5*0 2 c 10 5*0 2
  //   c 10 5*0 2 c 10 5*0 2 c 10 5*0 2 c 10 5*0 2 c 10 5*0 2 c 2 11 4*0 2 c 14 5*0 2 c 2 11 4*0 2 c 14 5*0
  //   2 c 2 11 4*0 2 c 14 5*0 2 c 2 11 4*0 2 c 14 5*0 2 c 2 11 4*0 2 c 14 5*0 2 c 2 11 4*0 2 c 14 5*0 2 c
  //   2 11 4*0 2 c 14 5*0 2 c 2 11 4*0 2 c 14 5*0 2 c 10 5*0 2 c 10 5*0 2 c 10 5*0 2 c 10 5*0 2 c 10 5*0 2
  //   c 10 5*0 2 c 10 5*0 2 c 10 5*0 2 c 10 5*0 2 c 10 5*0 2 c 10 5*0 2 c 10 5*0 2 c 10 5*0 2 c 10 5*0 2 c
  //   10 5*0 2 c 10 5*0 2 c 10 5*0 2 c 10 5*0 2 c 10 5*0 2 c 10 5*0 2 c 10 5*0 2 c 10 5*0 2 c 10 5*0 2 c
  //   10 5*0 2 c 10 5*0 2 c 10 5*0 2 c 10 5*0 2 c 10 5*0 2 c 10 5*0 2 c 10 5*0 2 c 10 5*0 2 c 10 5*0 2 c
  //   10 5*0 2 c 10 5*0 2 c 10 5*0 2 c 10 5*0 2 c 10 5*0 2 c 10 5*0 2 c 10 5*0 2 c 10 5*0 2 c 10 5*0 2 c
  //   10 5*0 2 c 10 5*0 2 c 10 5*0 2 c 10 5*0 2 c 10 5*0 2 c 10 5*0 2 c 10 5*0 2 c 11 5*0 2 c 11 5*0 2 c
  //   11 5*0 2 c 11 5*0 2 c 11 5*0 2 c 11 5*0 2 c 11 5*0 2 c 11 5*0 2 c 11 5*0 2 c 11 5*0 2 c 11 5*0 2 c
  //   11 5*0 2 c 11 5*0 2 c 11 5*0 2 c 11 5*0 2 c 11 5*0 2 c 0 14 4*0 2 c 0 14 4*0 2 c 0 14 4*0 2 c 0 14
  //   4*0 2 c 0 2 11 0 0 0 2 c 0 2 11 0 0 0 2 c 0 2 11 0 0 0 2 c 0 2 11 0 0 0 2 c 0 14 4*0 2 c 0 14 4*0 2
  //   c 0 14 4*0 2 c 0 14 4*0 2 c 0 2 11 0 0 0 2 c 0 2 11 0 0 0 2 c 0 2 11 0 0 0 2 c 0 2 11 0 0 0 2 c 0 14
  //   4*0 2 c 0 14 4*0 2 c 0 14 4*0 2 c 0 14 4*0 2 c 0 14 4*0 2 c 0 14 4*0 2 c 0 14 4*0 2 c 0 14 4*0 2 c 0
  //   2 11 0 0 0 2 c 0 2 11 0 0 0 2 c 0 2 11 0 0 0 2 c 0 2 11 0 0 0 2 c 0 2 11 0 0 0 2 c 0 2 11 0 0 0 2 c
  //   0 2 11 0 0 0 2 c 0 2 11 0 0 0 2 c 10 5*0 2 c 10 5*0 2 c 10 5*0 2 c 10 5*0 2 c 10 5*0 2 c 10 5*0 2 c
  //   10 5*0 2 c 10 5*0 2 c 10 5*0 2 c 10 5*0 2 c 10 5*0 2 c 10 5*0 2 c 10 5*0 2 c 10 5*0 2 c 10 5*0 2 c
  //   10 5*0 2 c 10 5*0 2 c 10 5*0 2 c 10 5*0 2 c 10 5*0 2 c 10 5*0 2 c 10 5*0 2 c 10 5*0 2 c 10 5*0 2 c
  //   10 5*0 2 c 10 5*0 2 c 10 5*0 2 c 10 5*0 2 c 10 5*0 2 c 10 5*0 2 c 10 5*0 2 c 10 5*0 2 c 2 11 4*0 2 c
  //   2 11 4*0 2 c 14 5*0 2 c 14 5*0 2 c 2 11 4*0 2 c 2 11 4*0 2 c 14 5*0 2 c 14 5*0 2 c 2 11 4*0 2 c 2 11
  //   4*0 2 c 14 5*0 2 c 14 5*0 2 c 2 11 4*0 2 c 2 11 4*0 2 c 14 5*0 2 c 14 5*0 2 c 10 5*0 2 c 10 5*0 2 c
  //   10 5*0 2 c 10 5*0 2 c 10 5*0 2 c 10 5*0 2 c 10 5*0 2 c 10 5*0 2 c 10 5*0 2 c 10 5*0 2 c 10 5*0 2 c
  //   10 5*0 2 c 10 5*0 2 c 10 5*0 2 c 10 5*0 2 c 10 5*0 2 c 10 5*0 2 c 10 5*0 2 c 10 5*0 2 c 10 5*0 2 c
  //   10 5*0 2 c 10 5*0 2 c 10 5*0 2 c 10 5*0 2 c 10 5*0 2 c 10 5*0 2 c 10 5*0 2 c 10 5*0 2 c 10 5*0 2 c
  //   10 5*0 2 c 10 5*0 2 c 10 5*0 2 c 11 5*0 2 c 11 5*0 2 c 11 5*0 2 c 11 5*0 2 c 11 5*0 2 c 11 5*0 2 c
  //   11 5*0 2 c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
  //   contents of rom_2 (hex, n*v repeats v):
  //   4 10 6*0 4 10 4 10 4*0 4 10 6*0 4 10 4 10 4*0 4 10 6*0 4 10 4 10 4*0 4 10 6*0 4 10 4 10 4*0 4 10 6*0
  //   4 10 4 10 4*0 4 10 6*0 4 10 4 10 4*0 4 10 6*0 4 10 4 10 4*0 4 10 6*0 4 10 4 10 4*0 4 10 6*0 4 10 6*0
  //   4 10 6*0 4 10 6*0 4 10 6*0 4 10 6*0 4 10 6*0 4 10 6*0 4 10 6*0 4 10 6*0 4 10 6*0 4 10 6*0 4 10 6*0 4
  //   10 6*0 4 10 6*0 4 10 6*0 4 10 6*0 4 10 6*0 4 10 6*0 4 10 6*0 4 10 6*0 4 10 6*0 4 10 6*0 4 10 6*0 4
  //   10 6*0 4 10 6*0 4 10 6*0 4 10 6*0 4 10 6*0 4 10 6*0 4 10 6*0 4 10 6*0 4 10 6*0 4 10 6*0 4 10 6*0 4
  //   10 6*0 4 10 6*0 4 10 6*0 4 10 6*0 4 10 6*0 4 10 6*0 4 10 6*0 4 10 6*0 4 10 6*0 4 10 6*0 4 10 6*0 4
  //   10 6*0 4 10 6*0 4 10 40 5*0 4 10 40 5*0 4 10 40 5*0 4 10 40 5*0 4 10 40 5*0 4 10 40 5*0 4 10 40 5*0
  //   4 10 40 5*0 4 10 40 5*0 4 10 40 5*0 4 10 40 5*0 4 10 40 5*0 4 10 40 5*0 4 10 40 5*0 4 10 40 5*0 4 10
  //   40 5*0 4 10 6*0 4 10 6*0 4 10 6*0 4 10 6*0 4 10 6*0 4 10 6*0 4 10 6*0 4 10 6*0 4 10 6*0 4 10 6*0 4
  //   10 6*0 4 10 6*0 4 10 6*0 4 10 6*0 4 10 6*0 4 10 6*0 4 10 6*0 4 10 6*0 4 10 6*0 4 10 6*0 4 10 6*0 4
  //   10 6*0 4 10 6*0 4 10 6*0 4 10 6*0 4 10 6*0 4 10 6*0 4 10 6*0 4 10 6*0 4 10 6*0 4 10 6*0 4 10 6*0 4
  //   10 4 10 4*0 4 10 4 10 4*0 4 10 4 10 4*0 4 10 4 10 4*0 4 10 4 10 4*0 4 10 4 10 4*0 4 10 4 10 4*0 4 10
  //   4 10 4*0 4 10 4 10 4 10 0 0 4 10 4 10 4 10 0 0 4 10 4 10 4 10 0 0 4 10 4 10 4 10 0 0 4 10 4 10 4 10
  //   0 0 4 10 4 10 4 10 0 0 4 10 4 10 4 10 0 0 4 10 4 10 4 10 0 0 4 10 6*0 4 10 6*0 4 10 6*0 4 10 6*0 4
  //   10 6*0 4 10 6*0 4 10 6*0 4 10 6*0 4 10 6*0 4 10 6*0 4 10 6*0 4 10 6*0 4 10 6*0 4 10 6*0 4 10 6*0 4
  //   10 6*0 4 10 4 10 4*0 4 10 6*0 4 10 4 10 4*0 4 10 6*0 4 10 4 10 4*0 4 10 6*0 4 10 4 10 4*0 4 10 6*0 4
  //   10 4 10 4*0 4 10 6*0 4 10 4 10 4*0 4 10 6*0 4 10 4 10 4*0 4 10 6*0 4 10 4 10 4*0 4 10 6*0 4 10 6*0 4
  //   10 6*0 4 10 6*0 4 10 6*0 4 10 6*0 4 10 6*0 4 10 6*0 4 10 6*0 4 10 6*0 4 10 6*0 4 10 6*0 4 10 6*0 4
  //   10 6*0 4 10 6*0 4 10 6*0 4 10 6*0 4 10 6*0 4 10 6*0 4 10 6*0 4 10 6*0 4 10 6*0 4 10 6*0 4 10 6*0 4
  //   10 6*0 4 10 6*0 4 10 6*0 4 10 6*0 4 10 6*0 4 10 6*0 4 10 6*0 4 10 6*0 4 10 6*0 4 10 40 5*0 4 10 40
  //   5*0 4 10 40 5*0 4 10 40 5*0 4 10 40 5*0 4 10 40 5*0 4 10 40 5*0 4 10 40 5*0 4 10 40 5*0 4 10 40 5*0
  //   4 10 40 5*0 4 10 40 5*0 4 10 40 5*0 4 10 40 5*0 4 10 40 5*0 4 10 40 5*0 4 10 6*0 4 10 6*0 4 10 6*0 4
  //   10 6*0 4 10 6*0 4 10 6*0 4 10 6*0 4 10 6*0 4 10 6*0 4 10 6*0 4 10 6*0 4 10 6*0 4 10 6*0 4 10 6*0 4
  //   10 6*0 4 10 6*0 4 10 2 5*0 4 10 2 5*0 4 10 2 5*0 4 10 2 5*0 4 10 2 4 10 0 0 0 4 10 2 4 10 0 0 0 4 10
  //   2 4 10 0 0 0 4 10 2 4 10 0 0 0 4 10 2 5*0 4 10 2 5*0 4 10 2 5*0 4 10 2 5*0 4 10 2 4 10 0 0 0 4 10 2
  //   4 10 0 0 0 4 10 2 4 10 0 0 0 4 10 2 4 10 0 0 0 4 10 6*0 4 10 6*0 4 10 6*0 4 10 6*0 4 10 6*0 4 10 6*0
  //   4 10 6*0 4 10 6*0 4 10 0 4 10 0 0 0 4 10 0 4 10 0 0 0 4 10 0 4 10 0 0 0 4 10 0 4 10 0 0 0 4 10 0 4
  //   10 0 0 0 4 10 0 4 10 0 0 0 4 10 0 4 10 0 0 0 4 10 0 4 10 0 0 0 4 10 6*0 4 10 6*0 4 10 6*0 4 10 6*0 4
  //   10 6*0 4 10 6*0 4 10 6*0 4 10 6*0 4 10 6*0 4 10 6*0 4 10 6*0 4 10 6*0 4 10 6*0 4 10 6*0 4 10 6*0 4
  //   10 6*0 4 10 6*0 4 10 6*0 4 10 6*0 4 10 6*0 4 10 6*0 4 10 6*0 4 10 6*0 4 10 6*0 4 10 6*0 4 10 6*0 4
  //   10 6*0 4 10 6*0 4 10 6*0 4 10 6*0 4 10 6*0 4 10 6*0 4 10 4 10 4*0 4 10 4 10 4*0 4 10 6*0 4 10 6*0 4
  //   10 4 10 4*0 4 10 4 10 4*0 4 10 6*0 4 10 6*0 4 10 4 10 4*0 4 10 4 10 4*0 4 10 6*0 4 10 6*0 4 10 4 10
  //   4*0 4 10 4 10 4*0 4 10 6*0 4 10 6*0 4 10 6*0 4 10 6*0 4 10 6*0 4 10 6*0 4 10 6*0 4 10 6*0 4 10 6*0 4
  //   10 6*0 4 10 6*0 4 10 6*0 4 10 6*0 4 10 6*0 4 10 6*0 4 10 6*0 4 10 6*0 4 10 6*0 4 10 40 5*0 4 10 40
  //   5*0 4 10 40 5*0 4 10 40 5*0 4 10 40 5*0 4 10 40 5*0 4 10 40 5*0 4 10 40 5*0 4 10 40 5*0 4 10 40 5*0
  //   4 10 40 5*0 4 10 40 5*0 4 10 40 5*0 4 10 40 5*0 4 10 40 5*0 4 10 40 5*0 4 10 6*0 4 10 6*0 4 10 6*0 4
  //   10 6*0 4 10 6*0 4 10 6*0 4 10 6*0 4 10 6*0 4 10 6*0 4 10 6*0 4 10 6*0 4 10 6*0 4 10 6*0 4 10 6*0 4
  //   10 6*0 4 10 6*0 4 10 2 5*0 4 10 2 5*0 4 10 2 5*0 4 10 2 5*0 4 10 2 4 10 0 0 0 4 10 2 4 10 0 0 0 4 10
  //   2 4 10 0 0 0 4 10 2 4 10 0 0 0 4 10 2 5*0 4 10 2 5*0 4 10 2 5*0 4 10 2 5*0 4 10 2 4 10 0 0 0 4 10 2
  //   4 10 0 0 0 4 10 2 4 10 0 0 0 4 10 2 4 10 0 0 0 4 10 6*0 4 10 6*0 4 10 6*0 4 10 6*0 4 10 6*0 4 10 6*0
  //   4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
  //   contents of rom_3 (hex, n*v repeats v):
  //   899*0 62 7*0 62 7*0 62 7*0 62 7*0 62 7*0 62 7*0 62 7*0 62 7*0 62 7*0 62 7*0 62 7*0 62 7*0 62 7*0 62
  //   7*0 62 7*0 62 774*0 62 7*0 62 7*0 62 7*0 62 7*0 62 7*0 62 7*0 62 7*0 62 7*0 62 7*0 62 7*0 62 7*0 62
  //   7*0 62 7*0 62 7*0 62 7*0 62 7*0 62 7*0 62 7*0 62 7*0 62 7*0 62 7*0 62 7*0 62 7*0 62 7*0 62 7*0 62
  //   7*0 62 7*0 62 7*0 62 7*0 62 7*0 62 7*0 62 775*0 62 7*0 62 7*0 62 7*0 62 7*0 62 7*0 62 7*0 62 7*0 62
  //   7*0 62 7*0 62 7*0 62 7*0 62 7*0 62 7*0 62 7*0 62 7*0 62 7*0 62 7*0 62 7*0 62 7*0 62 7*0 62 7*0 62
  //   7*0 62 7*0 62 7*0 62 7*0 62 7*0 62 7*0 62 7*0 62 7*0 62 7*0 62 7*0 62 775*0 62 7*0 62 7*0 62 7*0 62
  //   7*0 62 7*0 62 7*0 62 7*0 62 7*0 62 7*0 62 7*0 62 7*0 62 7*0 62 7*0 62 7*0 62 7*0 62 7*0 62 7*0 62
  //   7*0 62 7*0 62 7*0 62 7*0 62 7*0 62 7*0 62 7*0 62 7*0 62 7*0 62 7*0 62 7*0 62 7*0 62 7*0 62 7*0 62
  //   775*0 62 7*0 62 7*0 62 7*0 62 7*0 62 7*0 62 7*0 62 7*0 62 7*0 62 7*0 62 7*0 62 7*0 62 7*0 62 7*0 62
  //   7*0 62 7*0 62 7*0 62 7*0 62 7*0 62 7*0 62 7*0 62 7*0 62 7*0 62 7*0 62 7*0 62 7*0 62 7*0 62 7*0 62
  //   7*0 62 7*0 62 7*0 62 7*0 62 775*0 62 7*0 62 7*0 62 7*0 62 7*0 62 7*0 62 7*0 62 7*0 62 7*0 62 7*0 62
  //   7*0 62 7*0 62 7*0 62 7*0 62 7*0 62 7*0 62 7*0 62 7*0 62 7*0 62 7*0 62 7*0 62 7*0 62 7*0 62 7*0 62
  //   7*0 62 7*0 62 7*0 62 7*0 62 7*0 62 7*0 62 7*0 62 7*0 62 135*0 62 7*0 62 7*0 62 7*0 62 7*0 62 7*0 62
  //   7*0 62 7*0 62 7*0 62 7*0 62 7*0 62 7*0 62 7*0 62 7*0 62 7*0 62 7*0 62 7*0 62 7*0 62 7*0 62 7*0 62
  //   7*0 62 7*0 62 7*0 62 7*0 62 7*0 62 7*0 62 7*0 62 7*0 62 7*0 62 7*0 62 7*0 62 7*0 62 7*0 62 7*0 62
  //   7*0 62 7*0 62 7*0 62 7*0 62 7*0 62 7*0 62 7*0 62 7*0 62 7*0 62 7*0 62 7*0 62 7*0 62 7*0 62 7*0 62
  //   7*0 62 7*0 62 7*0 62 7*0 62 7*0 62 7*0 62 7*0 62 7*0 62 7*0 62 7*0 62 7*0 62 7*0 62 7*0 62 7*0 62
  //   7*0 62 7*0 62 7*0 62 7*0 62 7*0 62 7*0 62 7*0 62 7*0 62 7*0 62 7*0 62 7*0 62 7*0 62 7*0 62 7*0 62
  //   7*0 62 7*0 62 7*0 62 7*0 62 136*0 62 7*0 62 7*0 62 7*0 62 7*0 62 7*0 62 7*0 62 7*0 62 7*0 62 7*0 62
  //   7*0 62 7*0 62 7*0 62 7*0 62 7*0 62 7*0 62 775*0 62 7*0 62 7*0 62 7*0 62 7*0 62 7*0 62 7*0 62 7*0 62
  //   7*0 62 7*0 62 7*0 62 7*0 62 7*0 62 7*0 62 7*0 62 7*0 62 902*0 f9 4 6*0 f9 4 6*0 f9 4 6*0 f9 4 6*0 f9
  //   4 6*0 f9 4 6*0 f9 4 6*0 f9 4 6*0 f9 4 6*0 f9 4 6*0 f9 4 6*0 f9 4 6*0 f9 4 6*0 f9 4 6*0 f9 4 6*0 f9 4
  //   646*0 62 7*0 62 7*0 62 7*0 62 7*0 62 7*0 62 7*0 62 7*0 62 7*0 62 7*0 62 7*0 62 7*0 62 7*0 62 7*0 62
  //   7*0 62 7*0 62 135*0 f9 4 6*0 f9 4 6*0 f9 4 6*0 f9 4 6*0 f9 4 6*0 f9 4 6*0 f9 4 6*0 f9 4 6*0 f9 4 6*0
  //   f9 4 6*0 f9 4 6*0 f9 4 6*0 f9 4 6*0 f9 4 6*0 f9 4 6*0 f9 4 646*0 62 7*0 62 7*0 62 7*0 62 7*0 62 7*0
  //   62 7*0 62 7*0 62 7*0 62 7*0 62 7*0 62 7*0 62 7*0 62 7*0 62 7*0 62 7*0 62 135*0 f9 4 6*0 f9 4 6*0 f9
  //   4 6*0 f9 4 6*0 f9 4 6*0 f9 4 6*0 f9 4 6*0 f9 4 6*0 f9 4 6*0 f9 4 6*0 f9 4 6*0 f9 4 6*0 f9 4 6*0 f9 4
  //   6*0 f9 4 6*0 f9 4 646*0 62 7*0 62 7*0 62 7*0 62 7*0 62 7*0 62 7*0 62 7*0 62 7*0 62 7*0 62 7*0 62 7*0
  //   62 7*0 62 7*0 62 7*0 62 7*0 62 135*0 f9 4 6*0 f9 4 6*0 f9 4 6*0 f9 4 6*0 f9 4 6*0 f9 4 6*0 f9 4 6*0
  //   f9 4 6*0 f9 4 6*0 f9 4 6*0 f9 4 6*0 f9 4 6*0 f9 4 6*0 f9 4 6*0 f9 4 6*0 f9 4 646*0 62 7*0 62 7*0 62
  //   7*0 62 7*0 62 7*0 62 7*0 62 7*0 62 7*0 62 7*0 62 7*0 62 7*0 62 7*0 62 7*0 62 7*0 62 7*0 62 903*0 62
  //   7*0 62 7*0 62 7*0 62 7*0 62 7*0 62 7*0 62 7*0 62 7*0 62 7*0 62 7*0 62 7*0 62 7*0 62 7*0 62 7*0 62
  //   7*0 62 393*0 9 4 6*0 9 4 6*0 9 4 6*0 9 4 6*0 9 4 6*0 9 4 6*0 9 4 6*0 9 4 6*0 9 4 6*0 9 4 6*0 9 4 6*0
  //   9 4 6*0 9 4 6*0 9 4 6*0 9 4 6*0 9 4 6*0 9 4 6*0 9 4 6*0 9 4 6*0 9 4 6*0 9 4 6*0 9 4 6*0 9 4 6*0 9 4
  //   6*0 9 4 6*0 9 4 6*0 9 4 6*0 9 4 6*0 9 4 6*0 9 4 6*0 9 4 6*0 9 4 6*0 9 4 6*0 9 4 6*0 9 4 6*0 9 4 6*0
  //   9 4 6*0 9 4 6*0 9 4 6*0 9 4 6*0 9 4 6*0 9 4 6*0 9 4 6*0 9 4 6*0 9 4 6*0 9 4 6*0 9 4 6*0 9 4 6*0 9 4
  //   6*0 9 4 6*0 9 4 6*0 9 4 6*0 9 4 6*0 9 4 6*0 9 4 6*0 9 4 6*0 9 4 6*0 9 4 6*0 9 4 6*0 9 4 6*0 9 4 6*0
  //   9 4 6*0 9 4 6*0 9 4 134*0 9 4 6*0 9 4 6*0 9 4 6*0 9 4 6*0 9 4 6*0 9 4 6*0 9 4 6*0 9 4 6*0 9 4 6*0 9
  //   4 6*0 9 4 6*0 9 4 6*0 9 4 6*0 9 4 6*0 9 4 6*0 9 4 773*0 62 7*0 62 7*0 62 7*0 62 7*0 62 7*0 62 7*0 62
  //   7*0 62 7*0 62 7*0 62 7*0 62 7*0 62 7*0 62 7*0 62 7*0 62 7*0 62 134*0 f9 4 0 f9 4 0 0 0 f9 4 0 f9 4 0
  //   0 0 f9 4 0 f9 4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
  //   contents of rom_4 (hex, n*v repeats v):
  //   130*0 6 7*0 6 7*0 6 7*0 6 7*0 6 7*0 6 7*0 6 7*0 6 7*0 6 7*0 6 7*0 6 7*0 6 7*0 6 7*0 6 7*0 6 7*0 6
  //   7*0 12 7*0 12 7*0 12 7*0 12 7*0 12 7*0 12 7*0 12 7*0 12 7*0 12 7*0 12 7*0 12 7*0 12 7*0 12 7*0 12
  //   7*0 12 7*0 12 7*0 42 7*0 42 7*0 42 7*0 42 7*0 42 7*0 42 7*0 42 7*0 42 7*0 42 7*0 42 7*0 42 7*0 42
  //   7*0 42 7*0 42 7*0 42 7*0 42 7*0 2 7*0 2 7*0 2 7*0 2 7*0 2 7*0 2 7*0 2 7*0 2 7*0 2 7*0 2 7*0 2 7*0 2
  //   7*0 2 7*0 2 7*0 2 7*0 2 7*0 2 7*0 2 7*0 2 7*0 2 7*0 2 7*0 2 7*0 2 7*0 2 7*0 2 7*0 2 7*0 2 7*0 2 7*0
  //   2 7*0 2 7*0 2 7*0 2 263*0 9 7*0 9 7*0 9 7*0 9 7*0 9 7*0 9 7*0 9 7*0 9 7*0 9 7*0 9 7*0 9 7*0 9 7*0 9
  //   7*0 9 7*0 9 7*0 9 135*0 18 7*0 18 7*0 18 7*0 18 7*0 18 7*0 18 7*0 18 7*0 18 7*0 18 7*0 18 7*0 18 7*0
  //   18 7*0 18 7*0 18 7*0 18 7*0 18 7*0 48 7*0 48 7*0 48 7*0 48 7*0 48 7*0 48 7*0 48 7*0 48 7*0 48 7*0 48
  //   7*0 48 7*0 48 7*0 48 7*0 48 7*0 48 7*0 48 7*0 8 7*0 8 7*0 8 7*0 8 7*0 8 7*0 8 7*0 8 7*0 8 7*0 8 7*0
  //   8 7*0 8 7*0 8 7*0 8 7*0 8 7*0 8 7*0 8 7*0 8 7*0 8 7*0 8 7*0 8 7*0 8 7*0 8 7*0 8 7*0 8 7*0 8 7*0 8
  //   7*0 8 7*0 8 7*0 8 7*0 8 7*0 8 7*0 8 7*0 8 7*0 8 7*0 8 7*0 8 7*0 8 7*0 8 7*0 8 7*0 8 7*0 8 7*0 8 7*0
  //   8 7*0 8 7*0 8 7*0 8 7*0 8 7*0 8 7*0 8 7*0 8 7*0 8 7*0 8 7*0 8 7*0 8 7*0 8 7*0 8 7*0 8 7*0 8 7*0 8
  //   7*0 8 7*0 8 7*0 8 7*0 8 7*0 8 7*0 21 7*0 21 7*0 21 7*0 21 7*0 21 7*0 21 7*0 21 7*0 21 7*0 21 7*0 21
  //   7*0 21 7*0 21 7*0 21 7*0 21 7*0 21 7*0 21 7*0 24 7*0 24 7*0 24 7*0 24 7*0 24 7*0 24 7*0 24 7*0 24
  //   7*0 24 7*0 24 7*0 24 7*0 24 7*0 24 7*0 24 7*0 24 7*0 24 135*0 60 7*0 60 7*0 60 7*0 60 7*0 60 7*0 60
  //   7*0 60 7*0 60 7*0 60 7*0 60 7*0 60 7*0 60 7*0 60 7*0 60 7*0 60 7*0 60 7*0 20 7*0 20 7*0 20 7*0 20
  //   7*0 20 7*0 20 7*0 20 7*0 20 7*0 20 7*0 20 7*0 20 7*0 20 7*0 20 7*0 20 7*0 20 7*0 20 7*0 20 7*0 20
  //   7*0 20 7*0 20 7*0 20 7*0 20 7*0 20 7*0 20 7*0 20 7*0 20 7*0 20 7*0 20 7*0 20 7*0 20 7*0 20 7*0 20
  //   7*0 20 7*0 20 7*0 20 7*0 20 7*0 20 7*0 20 7*0 20 7*0 20 7*0 20 7*0 20 7*0 20 7*0 20 7*0 20 7*0 20
  //   7*0 20 7*0 20 7*0 20 7*0 20 7*0 20 7*0 20 7*0 20 7*0 20 7*0 20 7*0 20 7*0 20 7*0 20 7*0 20 7*0 20
  //   7*0 20 7*0 20 7*0 20 7*0 20 7*0 81 7*0 81 7*0 81 7*0 81 7*0 81 7*0 81 7*0 81 7*0 81 7*0 81 7*0 81
  //   7*0 81 7*0 81 7*0 81 7*0 81 7*0 81 7*0 81 7*0 84 7*0 84 7*0 84 7*0 84 7*0 84 7*0 84 7*0 84 7*0 84
  //   7*0 84 7*0 84 7*0 84 7*0 84 7*0 84 7*0 84 7*0 84 7*0 84 7*0 90 7*0 90 7*0 90 7*0 90 7*0 90 7*0 90
  //   7*0 90 7*0 90 7*0 90 7*0 90 7*0 90 7*0 90 7*0 90 7*0 90 7*0 90 7*0 90 135*0 80 7*0 80 7*0 80 7*0 80
  //   7*0 80 7*0 80 7*0 80 7*0 80 7*0 80 7*0 80 7*0 80 7*0 80 7*0 80 7*0 80 7*0 80 7*0 80 7*0 80 7*0 80
  //   7*0 80 7*0 80 7*0 80 7*0 80 7*0 80 7*0 80 7*0 80 7*0 80 7*0 80 7*0 80 7*0 80 7*0 80 7*0 80 7*0 80
  //   7*0 80 7*0 80 7*0 80 7*0 80 7*0 80 7*0 80 7*0 80 7*0 80 7*0 80 7*0 80 7*0 80 7*0 80 7*0 80 7*0 80
  //   7*0 80 7*0 80 7*0 80 7*0 80 7*0 80 7*0 80 7*0 80 7*0 80 7*0 80 7*0 80 7*0 80 7*0 80 7*0 80 7*0 80
  //   7*0 80 7*0 80 7*0 80 7*0 80 7*0 1 7*0 1 7*0 1 7*0 1 7*0 1 7*0 1 7*0 1 7*0 1 7*0 1 7*0 1 7*0 1 7*0 1
  //   7*0 1 7*0 1 7*0 1 7*0 1 7*0 4 7*0 4 7*0 4 7*0 4 7*0 4 7*0 4 7*0 4 7*0 4 7*0 4 7*0 4 7*0 4 7*0 4 7*0
  //   4 7*0 4 7*0 4 7*0 4 7*0 10 7*0 10 7*0 10 7*0 10 7*0 10 7*0 10 7*0 10 7*0 10 7*0 10 7*0 10 7*0 10 7*0
  //   10 7*0 10 7*0 10 7*0 10 7*0 10 7*0 40 7*0 40 7*0 40 7*0 40 7*0 40 7*0 40 7*0 40 7*0 40 7*0 40 7*0 40
  //   7*0 40 7*0 40 7*0 40 7*0 40 7*0 40 7*0 40 519*0 1 7*0 1 7*0 1 7*0 1 7*0 1 7*0 1 7*0 1 7*0 1 7*0 1
  //   7*0 1 7*0 1 7*0 1 7*0 1 7*0 1 7*0 1 7*0 1 7*0 4 7*0 4 7*0 4 7*0 4 7*0 4 7*0 4 7*0 4 7*0 4 7*0 4 7*0
  //   4 7*0 4 7*0 4 7*0 4 7*0 4 7*0 4 7*0 4 7*0 10 7*0 10 7*0 10 7*0 10 7*0 10 7*0 10 7*0 10 7*0 10 7*0 10
  //   7*0 10 7*0 10 7*0 10 7*0 10 7*0 10 7*0 10 7*0 10 7*0 40 7*0 40 7*0 40 7*0 40 7*0 40 7*0 40 7*0 40
  //   7*0 40 7*0 40 7*0 40 7*0 40 7*0 40 7*0 40 7*0 40 7*0 40 7*0 40 647*0 8 7*0 8 7*0 8 7*0 8 7*0 8 7*0 8
  //   7*0 8 7*0 8 7*0 8 7*0 8 7*0 8 7*0 8 7*0 8 7*0 8 7*0 8 7*0 8 7*0 20 7*0 20 7*0 20 7*0 20 7*0 20 7*0
  //   20 7*0 20 7*0 20 7*0 20 7*0 20 7*0 20 7*0 20 7*0 20 7*0 20 7*0 20 7*0 20 7*0 80 7*0 80 7*0 80 7*0 80
  //   7*0 80 7*0 80 7*0 80 7*0 80 7*0 80 7*0 80 7*0 80 7*0 80 7*0 80 7*0 80 7*0 80 7*0 80 520*0 1 7*0 1
  //   7*0 1 7*0 1 7*0 1 7*0 1 7*0 1 7*0 1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
  //   And so on.
  //   And another slice.
  //   This is one 8 bit "slice" of the output control signals.
endmodule

module ALU (
  input  [7:0] A,
  input  [7:0] B,
  input  carry_in,
  input  M,
  input  S0,
  input  S1,
  input  S2,
  input  S3,
  input  result_output_enable,
  input  clock,
  input  sim_only_reset,
  input  store_result,
  input  store_flags,
  output unclocked_zero,
  output clocked_zero,
  output unclocked_negative,
  output clocked_negative,
  output unclocked_carryborrow_out,
  output clocked_carryborrow_out,
  output unclocked_A___B,
  output clocked_A___B,
  output [7:0] tristate_clocked_result,
  output [7:0] unclocked_result,
  output [7:0] clocked_result
);

  wire n74ls181_1_a_b, n74ls181_1_carry_out_bar, n74ls181_2_a_b, n74ls181_2_carry_out_bar, not_2_out,
       or_1_out, or_2_out, or_3_out, or_4_out, or_5_out, or_6_out, or_7_out, safe_clock_enable_1_clock_out,
       safe_clock_enable_2_clock_out;

  and and_1 (unclocked_A___B, n74ls181_1_a_b, n74ls181_2_a_b);
  not not_1 (unclocked_carryborrow_out, n74ls181_2_carry_out_bar);
  not not_2 (not_2_out, carry_in);
  _74LS181 u_74ls181_1 (
    .B(B[3:0]), .A(A[3:0]), .M(M), .carry_in_bar(not_2_out), .carry_out_bar(n74ls181_1_carry_out_bar),
    .F(unclocked_result[3:0]), .A_B(n74ls181_1_a_b), .S0(S0), .S1(S1), .S2(S2), .S3(S3));  // open: Y, X
  _74LS181 u_74ls181_2 (
    .B(B[7:4]), .A(A[7:4]), .M(M), .carry_in_bar(n74ls181_1_carry_out_bar),
    .carry_out_bar(n74ls181_2_carry_out_bar), .F({unclocked_negative, unclocked_result[6:4]}),
    .A_B(n74ls181_2_a_b), .S0(S0), .S1(S1), .S2(S2), .S3(S3));  // open: Y, X
  or or_1 (or_1_out, unclocked_result[0], unclocked_result[1]);
  or or_2 (or_2_out, or_1_out, or_3_out);
  or or_3 (or_3_out, unclocked_result[2], unclocked_result[3]);
  or or_4 (or_4_out, unclocked_result[4], unclocked_result[5]);
  or or_5 (or_5_out, or_4_out, or_6_out);
  or or_6 (or_6_out, unclocked_result[6], unclocked_negative);
  safe_clock_enable safe_clock_enable_1 (
    .clock_enable(store_result), .clock_in(clock), .clock_out(safe_clock_enable_1_clock_out));
  safe_clock_enable safe_clock_enable_2 (
    .clock_enable(store_flags), .clock_in(clock), .clock_out(safe_clock_enable_2_clock_out));
  or or_7 (or_7_out, or_2_out, or_5_out);
  not not_3 (unclocked_zero, or_7_out);
  Register result (
    .D({unclocked_negative, unclocked_result[6:0]}), .en(1'b1), .Q(clocked_result),
    .clk(safe_clock_enable_1_clock_out), .clr(sim_only_reset));
  assign tristate_clocked_result = result_output_enable ? clocked_result : 8'bz;  // Controlled_Buffer controlled_buffer_1
  Register #(.width(4)) register_1 (
    .D({unclocked_A___B, unclocked_carryborrow_out, unclocked_negative, unclocked_zero}), .en(1'b1),
    .Q({clocked_A___B, clocked_carryborrow_out, clocked_negative, clocked_zero}),
    .clk(safe_clock_enable_2_clock_out), .clr(sim_only_reset));

  assign unclocked_result[7] = unclocked_negative;
endmodule

module register_bus_R (
  input  [7:0] \input ,
  input  input_enable,
  input  output_enable,
  input  clock,
  input  sim_only_reset,
  output [7:0] content,
  output [7:0] buffered_output
);

  wire safe_clock_enable_1_clock_out;

  safe_clock_enable safe_clock_enable_1 (
    .clock_enable(input_enable), .clock_in(clock), .clock_out(safe_clock_enable_1_clock_out));
  Register register_1 (.D(\input ), .en(1'b1), .Q(content), .clk(safe_clock_enable_1_clock_out), .clr(sim_only_reset));
  assign buffered_output = output_enable ? content : 8'bz;  // Controlled_Buffer controlled_buffer_1
endmodule

module register_bus_L (
  input  [7:0] \input ,
  input  output_enable,
  input  input_enable,
  input  clock,
  input  sim_only_reset,
  output [7:0] content,
  output [7:0] buffered_output
);

  wire safe_clock_enable_1_clock_out;

  safe_clock_enable safe_clock_enable_1 (
    .clock_enable(input_enable), .clock_in(clock), .clock_out(safe_clock_enable_1_clock_out));
  Register register_1 (.D(\input ), .en(1'b1), .Q(content), .clk(safe_clock_enable_1_clock_out), .clr(sim_only_reset));
  assign buffered_output = output_enable ? content : 8'bz;  // Controlled_Buffer controlled_buffer_1
endmodule

module program_counter (
  input  in,
  input  output_enable,
  input  [7:0] \input ,
  input  count,
  input  clock,
  input  reset,
  output [7:0] tristate_output,
  output [7:0] contents
);

  Counter counter_1 (.load(in), .D(\input ), .count(count), .Q(contents), .clk(clock), .clr(reset));  // open: carry
  assign tristate_output = output_enable ? contents : 8'bz;  // Controlled_Buffer controlled_buffer_1
endmodule

module _74LS181 (
  input  S0,
  input  S1,
  input  S2,
  input  S3,
  input  [3:0] B,
  input  [3:0] A,
  input  M,
  input  carry_in_bar,
  output Y,
  output carry_out_bar,
  output X,
  output [3:0] F,
  output A_B
);

  wire and_1_out, and_2_out, and_3_out, and_4_out, and_5_out, and_6_out, and_7_out, and_8_out, and_9_out,
       and_10_out, and_11_out, and_12_out, and_13_out, and_14_out, and_15_out, and_16_out, and_17_out,
       and_18_out, and_19_out, and_20_out, and_21_out, and_22_out, and_23_out, and_24_out, and_25_out,
       and_26_out, and_27_out, and_28_out, nand_1_out, nand_3_out, nor_1_out, nor_2_out, nor_3_out,
       nor_4_out, nor_5_out, nor_6_out, nor_7_out, nor_8_out, nor_10_out, nor_11_out, nor_12_out, not_1_out,
       not_2_out, not_3_out, not_4_out, not_5_out, xor_1_out, xor_2_out, xor_3_out, xor_4_out;

  not not_1 (not_1_out, B[3]);
  not not_2 (not_2_out, B[2]);
  not not_3 (not_3_out, B[1]);
  not not_4 (not_4_out, B[0]);
  not not_5 (not_5_out, M);
  and and_1 (and_1_out, B[3], S3, A[3]);
  and and_2 (and_2_out, A[3], S2, not_1_out);
  and and_3 (and_3_out, not_1_out, S1);
  and and_4 (and_4_out, S0, B[3]);
  and and_5 (and_5_out, B[2], S3, A[2]);
  and and_6 (and_6_out, A[2], S2, not_2_out);
  and and_7 (and_7_out, not_2_out, S1);
  and and_8 (and_8_out, S0, B[2]);
  and and_9 (and_9_out, B[1], S3, A[1]);
  and and_10 (and_10_out, A[1], S2, not_3_out);
  and and_11 (and_11_out, not_3_out, S1);
  and and_12 (and_12_out, S0, B[1]);
  and and_13 (and_13_out, B[0], S3, A[0]);
  and and_14 (and_14_out, A[0], S2, not_4_out);
  and and_15 (and_15_out, not_4_out, S1);
  and and_16 (and_16_out, S0, B[0]);
  nor nor_1 (nor_1_out, and_1_out, and_2_out);
  nor nor_2 (nor_2_out, and_3_out, and_4_out, A[3]);
  nor nor_3 (nor_3_out, and_5_out, and_6_out);
  nor nor_4 (nor_4_out, and_7_out, and_8_out, A[2]);
  nor nor_5 (nor_5_out, and_9_out, and_10_out);
  nor nor_6 (nor_6_out, and_11_out, and_12_out, A[1]);
  nor nor_7 (nor_7_out, and_13_out, and_14_out);
  nor nor_8 (nor_8_out, and_15_out, and_16_out, A[0]);
  xor xor_1 (xor_1_out, nor_1_out, nor_2_out);
  xor xor_2 (xor_2_out, nor_3_out, nor_4_out);
  xor xor_3 (xor_3_out, nor_5_out, nor_6_out);
  xor xor_4 (xor_4_out, nor_7_out, nor_8_out);
  and and_17 (and_17_out, nor_1_out, nor_4_out);
  and and_18 (and_18_out, nor_1_out, nor_3_out, nor_6_out);
  and and_19 (and_19_out, nor_1_out, nor_3_out, nor_5_out, nor_8_out);
  nand nand_1 (nand_1_out, nor_1_out, nor_3_out, nor_5_out, nor_7_out, carry_in_bar);
  nand nand_2 (X, nor_1_out, nor_3_out, nor_5_out, nor_7_out);
  and and_20 (and_20_out, carry_in_bar, nor_7_out, nor_5_out, nor_3_out, not_5_out);
  and and_21 (and_21_out, nor_5_out, nor_3_out, nor_8_out, not_5_out);
  and and_22 (and_22_out, nor_3_out, nor_6_out, not_5_out);
  and and_23 (and_23_out, nor_4_out, not_5_out);
  and and_24 (and_24_out, carry_in_bar, nor_7_out, nor_5_out, not_5_out);
  and and_25 (and_25_out, nor_5_out, nor_8_out, not_5_out);
  and and_26 (and_26_out, nor_6_out, not_5_out);
  and and_27 (and_27_out, carry_in_bar, nor_7_out, not_5_out);
  and and_28 (and_28_out, nor_8_out, not_5_out);
  nand nand_3 (nand_3_out, carry_in_bar, not_5_out);
  nor nor_9 (Y, nor_2_out, and_17_out, and_18_out, and_19_out);
  nor nor_10 (nor_10_out, and_20_out, and_21_out, and_22_out, and_23_out);
  nor nor_11 (nor_11_out, and_24_out, and_25_out, and_26_out);
  nor nor_12 (nor_12_out, and_27_out, and_28_out);
  or or_1 (carry_out_bar, ~Y, ~nand_1_out);  // OR_Gate
  xor xor_5 (F[3], xor_1_out, nor_10_out);
  xor xor_6 (F[2], xor_2_out, nor_11_out);
  xor xor_7 (F[1], xor_3_out, nor_12_out);
  xor xor_8 (F[0], xor_4_out, nand_3_out);
  and and_29 (A_B, F[3], F[2], F[1], F[0]);
endmodule

module safe_clock_enable (
  input  clock_enable,
  input  clock_in,
  output clock_out
);

  wire nor_1_out, nor_2_out, not_1_out, not_2_out;

  not not_1 (not_1_out, clock_enable);
  not not_2 (not_2_out, clock_in);
  nor nor_1 (nor_1_out, not_1_out, nor_2_out);
  nor nor_2 (nor_2_out, nor_1_out, not_2_out);
  and and_1 (clock_out, nor_1_out, clock_in);
endmodule

module schem_export (
  input  Halt,
  input  Reset,
  input  Auto_Manual,
  input  Manual_clock,
  output Clock,
  output Control_Clock
);

  wire Auto_clock_out, nand_1_out, nand_2_out, nand_3_out, nand_4_out, nand_5_out, nand_6_out, nand_7_out,
       nand_8_out, nor_1_out, nor_2_out, nor_3_out, nor_4_out, not_1_out, not_2_out;

  Clock_part Auto_clock (.out(Auto_clock_out));
  nand nand_1 (nand_1_out, Auto_Manual, Auto_Manual);
  nor nor_1 (nor_1_out, Halt, Reset);
  nand nand_2 (nand_2_out, Auto_Manual, Manual_clock);
  nand nand_3 (nand_3_out, nand_1_out, Auto_clock_out);
  nand nand_4 (nand_4_out, nor_1_out, nor_1_out);
  nand nand_5 (nand_5_out, nand_2_out, nand_3_out);
  nor nor_2 (nor_2_out, nand_5_out, nand_5_out);
  nor nor_3 (nor_3_out, nand_4_out, nor_4_out);
  nor nor_4 (nor_4_out, nor_3_out, nor_2_out);
  nand nand_6 (nand_6_out, nor_3_out, nand_5_out);
  nand nand_7 (nand_7_out, nand_6_out, nand_6_out);
  nand nand_8 (nand_8_out, nand_7_out, nand_7_out);
  J_K_Flip_Flop j_k_ff_1 (
    .J(1'b1), .clk(nand_7_out), .K(1'b1), .Q(Clock), .preset(1'b0), .en(1'b1), .reset(not_1_out));  // open: Qn
  not not_1 (not_1_out, nor_1_out);
  J_K_Flip_Flop j_k_ff_2 (
    .J(1'b1), .clk(nand_8_out), .K(1'b1), .Q(Control_Clock), .preset(1'b0), .en(1'b1), .reset(not_2_out));  // open: Qn
  not not_2 (not_2_out, nor_1_out);

  // Notes on the sheet:
  //   Safe clock enable
endmodule

module clipboard (
  input  in_1,
  input  in_2,
  output out_3,
  output out_4,
  output out_5,
  output clock_out
);

  wire A_IN, A_OUT, ACC_IN, ACC_OUT, ALU_A_IS_BUS, ALU_C_IN, ALU_CARRYBORROW_FLAG_CLOCKED,
       ALU_CARRYBORROW_FLAG_IMM, ALU_EQUAL_FLAG_CLOCKED, ALU_EQUAL_FLAG_IMM, ALU_M,
       ALU_NEGATIVE_FLAG_CLOCKED, ALU_NEGATIVE_FLAG_IMM, ALU_OUT, ALU_S0, ALU_S1, ALU_S2, ALU_S3,
       ALU_STORE_FLAGS, ALU_STORE_RESULT, ALU_ZERO_FLAG_CLOCKED, ALU_ZERO_FLAG_IMM, B_IN, B_OUT, C_IN, C_OUT,
       CLOCK_HALT, CONTROL_CLOCK, CU_CARRYBORROW_MIRROR, CU_EQUAL_MIRROR, CU_NEGATIVE_MIRROR, CU_STEP_RESET,
       CU_ZERO_MIRROR, IR_IN, MAR_IN, PC_COUNT, PC_IN, PC_OUT, SIM_ONLY_RESET, SP_IN, SP_OUT;
  wire [2:0] CU_MICROCODE_STEP;
  wire [7:0] A, ACC, ADDRESS, ALU_RESULT_CLOCKED, ALU_RESULT_IMM, B, BUS, C, CU_INSTRUCTION_MIRROR, IR, PC,
       SP;

  Button button_1 (.out(SIM_ONLY_RESET));
  LED led_1 (.in(ACC_IN));
  LED led_2 (.in(ACC_OUT));
  LED led_3 (.in(A_IN));
  LED led_4 (.in(A_OUT));
  LED led_5 (.in(B_IN));
  LED led_6 (.in(B_OUT));
  LED led_7 (.in(C_IN));
  LED led_8 (.in(C_OUT));
  LED led_9 (.in(ALU_STORE_RESULT));
  LED led_10 (.in(ALU_STORE_FLAGS));
  LED led_11 (.in(ALU_OUT));
  LED led_12 (.in(ALU_A_IS_BUS));
  LED led_13 (.in(ALU_S0));
  LED led_14 (.in(ALU_S1));
  LED led_15 (.in(ALU_S2));
  LED led_16 (.in(ALU_S3));
  LED led_17 (.in(ALU_M));
  LED led_18 (.in(ALU_C_IN));
  LED led_19 (.in(MAR_IN));
  LED led_20 (.in(out_4));
  LED led_21 (.in(out_5));
  LED led_22 (.in(out_3));
  LED led_23 (.in(SP_IN));
  LED led_24 (.in(SP_OUT));
  LED led_25 (.in(PC_IN));
  LED led_26 (.in(PC_OUT));
  LED led_27 (.in(PC_COUNT));
  LED led_28 (.in(IR_IN));
  LED led_29 (.in(CU_STEP_RESET));
  LED led_30 (.in(CLOCK_HALT));
  LED led_31 (.in(BUS[6]));
  LED led_32 (.in(BUS[7]));
  LED led_33 (.in(PC[7]));
  LED led_34 (.in(PC[6]));
  LED led_35 (.in(IR[6]));
  LED led_36 (.in(IR[7]));
  LED led_37 (.in(SP[7]));
  LED led_38 (.in(SP[6]));
  LED led_39 (.in(ACC[7]));
  LED led_40 (.in(ACC[6]));
  LED led_41 (.in(A[6]));
  LED led_42 (.in(A[7]));
  LED led_43 (.in(B[7]));
  LED led_44 (.in(B[6]));
  LED led_45 (.in(C[7]));
  LED led_46 (.in(C[6]));
  LED led_47 (.in(ADDRESS[7]));
  LED led_48 (.in(ADDRESS[6]));
  LED led_49 (.in(BUS[3]));
  LED led_50 (.in(BUS[4]));
  LED led_51 (.in(BUS[5]));
  LED led_52 (.in(BUS[2]));
  LED led_53 (.in(PC[5]));
  LED led_54 (.in(PC[4]));
  LED led_55 (.in(PC[3]));
  LED led_56 (.in(PC[2]));
  LED led_57 (.in(IR[4]));
  LED led_58 (.in(IR[2]));
  LED led_59 (.in(IR[3]));
  LED led_60 (.in(IR[5]));
  LED led_61 (.in(SP[5]));
  LED led_62 (.in(SP[2]));
  LED led_63 (.in(SP[3]));
  LED led_64 (.in(SP[4]));
  LED led_65 (.in(ACC[5]));
  LED led_66 (.in(ACC[2]));
  LED led_67 (.in(ACC[4]));
  LED led_68 (.in(ACC[3]));
  LED led_69 (.in(A[5]));
  LED led_70 (.in(A[2]));
  LED led_71 (.in(A[3]));
  LED led_72 (.in(A[4]));
  LED led_73 (.in(B[2]));
  LED led_74 (.in(B[4]));
  LED led_75 (.in(B[5]));
  LED led_76 (.in(B[3]));
  LED led_77 (.in(C[2]));
  LED led_78 (.in(C[5]));
  LED led_79 (.in(C[4]));
  LED led_80 (.in(C[3]));
  LED led_81 (.in(ADDRESS[3]));
  LED led_82 (.in(ADDRESS[4]));
  LED led_83 (.in(ADDRESS[2]));
  LED led_84 (.in(ADDRESS[5]));
  // Probe on BUS
  LED led_85 (.in(BUS[0]));
  LED led_86 (.in(BUS[1]));
  // Probe on PC
  LED led_87 (.in(PC[0]));
  LED led_88 (.in(PC[1]));
  // Probe on IR
  LED led_89 (.in(IR[1]));
  LED led_90 (.in(IR[0]));
  // Probe on SP
  LED led_91 (.in(SP[0]));
  LED led_92 (.in(SP[1]));
  // Probe on ACC
  LED led_93 (.in(ACC[1]));
  LED led_94 (.in(ACC[0]));
  // Probe on A
  LED led_95 (.in(A[0]));
  LED led_96 (.in(A[1]));
  // Probe on B
  LED led_97 (.in(B[0]));
  LED led_98 (.in(B[1]));
  // Probe on C
  LED led_99 (.in(C[0]));
  LED led_100 (.in(C[1]));
  // Probe on ADDRESS
  LED led_101 (.in(ADDRESS[0]));
  LED led_102 (.in(ADDRESS[1]));
  // Probe on BUS
  // Probe on BUS
  // Probe on PC
  // Probe on PC
  // Probe on IR
  // Probe on IR
  // Probe on SP
  // Probe on SP
  // Probe on ACC
  // Probe on ACC
  // Probe on A
  // Probe on A
  // Probe on B
  // Probe on B
  // Probe on C
  // Probe on C
  // Probe on ADDRESS
  // Probe on ADDRESS
  LED led_103 (.in(ALU_RESULT_IMM[6]));
  LED led_104 (.in(ALU_RESULT_IMM[7]));
  LED led_105 (.in(ALU_RESULT_CLOCKED[6]));
  LED led_106 (.in(ALU_RESULT_CLOCKED[7]));
  LED led_107 (.in(ALU_ZERO_FLAG_IMM));
  LED led_108 (.in(ALU_NEGATIVE_FLAG_IMM));
  LED led_109 (.in(ALU_CARRYBORROW_FLAG_IMM));
  LED led_110 (.in(ALU_EQUAL_FLAG_IMM));
  LED led_111 (.in(ALU_ZERO_FLAG_CLOCKED));
  LED led_112 (.in(ALU_NEGATIVE_FLAG_CLOCKED));
  LED led_113 (.in(ALU_CARRYBORROW_FLAG_CLOCKED));
  LED led_114 (.in(ALU_EQUAL_FLAG_CLOCKED));
  LED led_115 (.in(CU_INSTRUCTION_MIRROR[7]));
  LED led_116 (.in(CU_MICROCODE_STEP[2]));
  LED led_117 (.in(CU_ZERO_MIRROR));
  LED led_118 (.in(CU_NEGATIVE_MIRROR));
  LED led_119 (.in(CU_CARRYBORROW_MIRROR));
  LED led_120 (.in(CU_EQUAL_MIRROR));
  LED led_121 (.in(clock_out));
  LED led_122 (.in(CONTROL_CLOCK));
  LED led_123 (.in(ALU_RESULT_IMM[4]));
  LED led_124 (.in(ALU_RESULT_IMM[2]));
  LED led_125 (.in(ALU_RESULT_IMM[3]));
  LED led_126 (.in(ALU_RESULT_IMM[5]));
  LED led_127 (.in(ALU_RESULT_CLOCKED[2]));
  LED led_128 (.in(ALU_RESULT_CLOCKED[4]));
  LED led_129 (.in(ALU_RESULT_CLOCKED[5]));
  LED led_130 (.in(ALU_RESULT_CLOCKED[3]));
  LED led_131 (.in(CU_INSTRUCTION_MIRROR[6]));
  LED led_132 (.in(CU_INSTRUCTION_MIRROR[3]));
  LED led_133 (.in(CU_INSTRUCTION_MIRROR[5]));
  LED led_134 (.in(CU_INSTRUCTION_MIRROR[4]));
  LED led_135 (.in(CU_MICROCODE_STEP[1]));
  LED led_136 (.in(CU_MICROCODE_STEP[0]));
  // Probe on ALU_RESULT_IMM
  LED led_137 (.in(ALU_RESULT_IMM[0]));
  LED led_138 (.in(ALU_RESULT_IMM[1]));
  // Probe on ALU_RESULT_CLOCKED
  LED led_139 (.in(ALU_RESULT_CLOCKED[0]));
  LED led_140 (.in(ALU_RESULT_CLOCKED[1]));
  LED led_141 (.in(CU_INSTRUCTION_MIRROR[1]));
  LED led_142 (.in(CU_INSTRUCTION_MIRROR[2]));
  LED led_143 (.in(CU_INSTRUCTION_MIRROR[0]));
  // Probe on ALU_RESULT_IMM
  // Probe on ALU_RESULT_IMM
  // Probe on ALU_RESULT_CLOCKED
  // Probe on ALU_RESULT_CLOCKED
  // Probe on CU_INSTRUCTION_MIRROR
  // Probe on CU_INSTRUCTION_MIRROR
  // Probe on CU_INSTRUCTION_MIRROR
  // Probe on CU_MICROCODE_STEP
  // Probe on CU_MICROCODE_STEP
  // Probe on CU_MICROCODE_STEP

  // Other names for the same wires on the sheet: DATA_CLOCK = clock_out; EXT_CLOCK_PULSE = in_2;
  //   PROG_DATA_MEM = out_3; READ_FROM_MEM = out_5; RESET = in_1; WRITE_TO_MEM = out_4

  // Notes on the sheet:
  //   BIN
  //   BIN
  //   HEX
  //   BIN
  //   HEX
  //   DEC
  //   BIN
  //   HEX
  //   DEC
  //   BIN
  //   HEX
  //   DEC
  //   HEX
  //   DEC
  //   BIN
  //   HEX
  //   DEC
  //   BIN
  //   HEX
  //   DEC
  //   BIN
  //   HEX
  //   DEC
  //   DEC
  //   BIN
  //   HEX
  //   DEC
  //   BIN
  //   HEX
  //   DEC
  //   BIN
  //   HEX
  //   DEC
  //   BIN
  //   HEX
  //   DEC
  //   BIN
  //   HEX
  //   DEC
endmodule
